// Logisim project project2.circ as structural Verilog: 6 circuits, main circuit 1-bit Full Adder
module _1_bit_Full_Adder (
  input  a,
  input  b,
  input  CarryIn,
  output CarryOut,
  output Sum,
  output Generate,
  output Propagate
);

  wire and_1_out, and_2_out, and_3_out, and_4_out, and_5_out, and_6_out, and_7_out, not_1_out, not_2_out,
       not_3_out, not_4_out, not_5_out, not_6_out;

  and and_1 (and_1_out, b, CarryIn);
  and and_2 (and_2_out, a, CarryIn);
  and and_3 (and_3_out, a, b);
  not not_1 (not_1_out, a);
  not not_2 (not_2_out, b);
  not not_3 (not_3_out, a);
  not not_4 (not_4_out, CarryIn);
  not not_5 (not_5_out, b);
  not not_6 (not_6_out, CarryIn);
  or or_1 (CarryOut, and_1_out, and_2_out, and_3_out);
  and and_4 (and_4_out, not_1_out, not_2_out, CarryIn);
  and and_5 (and_5_out, not_3_out, b, not_4_out);
  and and_6 (and_6_out, a, not_5_out, not_6_out);
  and and_7 (and_7_out, a, b, CarryIn);
  and and_8 (Generate, a, b);
  or or_2 (Propagate, a, b);
  or or_3 (Sum, and_4_out, and_5_out, and_6_out, and_7_out);
endmodule

module _16_bit_ripple_carry_adder__2_s_complement (
  input  CarryIn,
  input  [15:0] a,
  input  [15:0] b,
  output [15:0] out_4,
  output overflow
);

  wire n1_bit_full_adder_1_carryout, n1_bit_full_adder_2_carryout, n1_bit_full_adder_3_carryout,
       n1_bit_full_adder_4_carryout, n1_bit_full_adder_5_carryout, n1_bit_full_adder_6_carryout,
       n1_bit_full_adder_7_carryout, n1_bit_full_adder_8_carryout, n1_bit_full_adder_9_carryout,
       n1_bit_full_adder_10_carryout, n1_bit_full_adder_11_carryout, n1_bit_full_adder_12_carryout,
       n1_bit_full_adder_13_carryout, n1_bit_full_adder_14_carryout, n1_bit_full_adder_15_carryout,
       n1_bit_full_adder_16_carryout;

  _1_bit_Full_Adder u_1_bit_full_adder_1 (
    .a(a[0]), .b(b[0]), .CarryIn(CarryIn), .CarryOut(n1_bit_full_adder_1_carryout), .Sum(out_4[0]));  // open: Generate, Propagate
  _1_bit_Full_Adder u_1_bit_full_adder_2 (
    .a(a[1]), .b(b[1]), .CarryIn(n1_bit_full_adder_1_carryout), .CarryOut(n1_bit_full_adder_2_carryout),
    .Sum(out_4[1]));  // open: Generate, Propagate
  _1_bit_Full_Adder u_1_bit_full_adder_3 (
    .a(a[2]), .b(b[2]), .CarryIn(n1_bit_full_adder_2_carryout), .CarryOut(n1_bit_full_adder_3_carryout),
    .Sum(out_4[2]));  // open: Generate, Propagate
  _1_bit_Full_Adder u_1_bit_full_adder_4 (
    .a(a[3]), .b(b[3]), .CarryIn(n1_bit_full_adder_3_carryout), .CarryOut(n1_bit_full_adder_4_carryout),
    .Sum(out_4[3]));  // open: Generate, Propagate
  _1_bit_Full_Adder u_1_bit_full_adder_5 (
    .a(a[4]), .b(b[4]), .CarryIn(n1_bit_full_adder_4_carryout), .CarryOut(n1_bit_full_adder_5_carryout),
    .Sum(out_4[4]));  // open: Generate, Propagate
  _1_bit_Full_Adder u_1_bit_full_adder_6 (
    .a(a[5]), .b(b[5]), .CarryIn(n1_bit_full_adder_5_carryout), .CarryOut(n1_bit_full_adder_6_carryout),
    .Sum(out_4[5]));  // open: Generate, Propagate
  _1_bit_Full_Adder u_1_bit_full_adder_7 (
    .a(a[6]), .b(b[6]), .CarryIn(n1_bit_full_adder_6_carryout), .CarryOut(n1_bit_full_adder_7_carryout),
    .Sum(out_4[6]));  // open: Generate, Propagate
  _1_bit_Full_Adder u_1_bit_full_adder_8 (
    .a(a[7]), .b(b[7]), .CarryIn(n1_bit_full_adder_7_carryout), .CarryOut(n1_bit_full_adder_8_carryout),
    .Sum(out_4[7]));  // open: Generate, Propagate
  _1_bit_Full_Adder u_1_bit_full_adder_9 (
    .a(a[8]), .b(b[8]), .CarryIn(n1_bit_full_adder_8_carryout), .CarryOut(n1_bit_full_adder_9_carryout),
    .Sum(out_4[8]));  // open: Generate, Propagate
  _1_bit_Full_Adder u_1_bit_full_adder_10 (
    .a(a[9]), .b(b[9]), .CarryIn(n1_bit_full_adder_9_carryout), .CarryOut(n1_bit_full_adder_10_carryout),
    .Sum(out_4[9]));  // open: Generate, Propagate
  _1_bit_Full_Adder u_1_bit_full_adder_11 (
    .a(a[10]), .b(b[10]), .CarryIn(n1_bit_full_adder_10_carryout), .CarryOut(n1_bit_full_adder_11_carryout),
    .Sum(out_4[10]));  // open: Generate, Propagate
  _1_bit_Full_Adder u_1_bit_full_adder_12 (
    .a(a[11]), .b(b[11]), .CarryIn(n1_bit_full_adder_11_carryout), .CarryOut(n1_bit_full_adder_12_carryout),
    .Sum(out_4[11]));  // open: Generate, Propagate
  _1_bit_Full_Adder u_1_bit_full_adder_13 (
    .a(a[12]), .b(b[12]), .CarryIn(n1_bit_full_adder_12_carryout), .CarryOut(n1_bit_full_adder_13_carryout),
    .Sum(out_4[12]));  // open: Generate, Propagate
  _1_bit_Full_Adder u_1_bit_full_adder_14 (
    .a(a[13]), .b(b[13]), .CarryIn(n1_bit_full_adder_13_carryout), .CarryOut(n1_bit_full_adder_14_carryout),
    .Sum(out_4[13]));  // open: Generate, Propagate
  _1_bit_Full_Adder u_1_bit_full_adder_15 (
    .a(a[14]), .b(b[14]), .CarryIn(n1_bit_full_adder_14_carryout), .CarryOut(n1_bit_full_adder_15_carryout),
    .Sum(out_4[14]));  // open: Generate, Propagate
  _1_bit_Full_Adder u_1_bit_full_adder_16 (
    .a(a[15]), .b(b[15]), .CarryIn(n1_bit_full_adder_15_carryout), .CarryOut(n1_bit_full_adder_16_carryout),
    .Sum(out_4[15]));  // open: Generate, Propagate
  xor xor_1 (overflow, n1_bit_full_adder_15_carryout, n1_bit_full_adder_16_carryout);
endmodule

module _4_bit_Adder (
  input  [3:0] A,
  input  [3:0] B,
  input  CarryIn,
  output P,
  output G,
  output [3:0] out_6
);

  wire and_2_out, and_3_out, and_4_out, carry_logic_1_c1, carry_logic_1_c2, carry_logic_1_c3,
       n1_bit_full_adder_1_generate, n1_bit_full_adder_1_propagate, n1_bit_full_adder_2_generate,
       n1_bit_full_adder_2_propagate, n1_bit_full_adder_3_generate, n1_bit_full_adder_3_propagate,
       n1_bit_full_adder_4_generate, n1_bit_full_adder_4_propagate;

  _1_bit_Full_Adder u_1_bit_full_adder_1 (
    .a(A[0]), .b(B[0]), .CarryIn(CarryIn), .Sum(out_6[0]), .Generate(n1_bit_full_adder_1_generate),
    .Propagate(n1_bit_full_adder_1_propagate));  // open: CarryOut
  _1_bit_Full_Adder u_1_bit_full_adder_2 (
    .a(A[1]), .b(B[1]), .CarryIn(carry_logic_1_c1), .Sum(out_6[1]), .Generate(n1_bit_full_adder_2_generate),
    .Propagate(n1_bit_full_adder_2_propagate));  // open: CarryOut
  _1_bit_Full_Adder u_1_bit_full_adder_3 (
    .a(A[2]), .b(B[2]), .CarryIn(carry_logic_1_c2), .Sum(out_6[2]), .Generate(n1_bit_full_adder_3_generate),
    .Propagate(n1_bit_full_adder_3_propagate));  // open: CarryOut
  _1_bit_Full_Adder u_1_bit_full_adder_4 (
    .a(A[3]), .b(B[3]), .CarryIn(carry_logic_1_c3), .Sum(out_6[3]), .Generate(n1_bit_full_adder_4_generate),
    .Propagate(n1_bit_full_adder_4_propagate));  // open: CarryOut
  Carry_Logic carry_logic_1 (
    .g0(n1_bit_full_adder_1_generate), .g1(n1_bit_full_adder_2_generate), .g2(n1_bit_full_adder_3_generate),
    .g3(n1_bit_full_adder_4_generate), .p0(n1_bit_full_adder_1_propagate),
    .p1(n1_bit_full_adder_2_propagate), .p2(n1_bit_full_adder_3_propagate),
    .p3(n1_bit_full_adder_4_propagate), .c0(CarryIn), .c1(carry_logic_1_c1), .c2(carry_logic_1_c2),
    .c3(carry_logic_1_c3));  // open: c4
  and and_1 (P, n1_bit_full_adder_4_propagate, n1_bit_full_adder_3_propagate, n1_bit_full_adder_2_propagate, n1_bit_full_adder_1_propagate);
  and and_2 (and_2_out, n1_bit_full_adder_4_propagate, n1_bit_full_adder_3_generate);
  or or_1 (G, n1_bit_full_adder_4_generate, and_2_out, and_3_out, and_4_out);
  and and_3 (and_3_out, n1_bit_full_adder_4_propagate, n1_bit_full_adder_3_propagate, n1_bit_full_adder_2_generate);
  and and_4 (and_4_out, n1_bit_full_adder_4_propagate, n1_bit_full_adder_3_propagate, n1_bit_full_adder_2_generate, n1_bit_full_adder_1_generate);
endmodule

module Carry_Logic (
  input  g0,
  input  g1,
  input  g2,
  input  g3,
  input  p0,
  input  p1,
  input  p2,
  input  p3,
  input  c0,
  output c1,
  output c2,
  output c3,
  output c4
);

  wire and_1_out, and_2_out, and_3_out, and_4_out, and_5_out, and_6_out, and_7_out, and_8_out, and_9_out,
       and_10_out;

  and and_1 (and_1_out, p0, c0);
  and and_2 (and_2_out, p1, g0);
  and and_3 (and_3_out, p2, p1, c0);
  and and_4 (and_4_out, p2, g1);
  and and_5 (and_5_out, p2, p1, g0);
  and and_6 (and_6_out, p2, p1, p0, c0);
  and and_7 (and_7_out, p3, g2);
  and and_8 (and_8_out, p3, p2, g1);
  and and_9 (and_9_out, p3, p2, p1, g0);
  and and_10 (and_10_out, p3, p2, p1, p0, c0);
  or or_1 (c1, g0, and_1_out);
  or or_2 (c2, g1, and_2_out, and_3_out);
  or or_3 (c3, g2, and_4_out, and_5_out, and_6_out);
  or or_4 (c4, g3, and_7_out, and_8_out, and_9_out, and_10_out);
endmodule

module _16_Bit_Carry_Lookahead_Adder (
  input  [15:0] A,
  input  [15:0] B,
  input  C_in,
  output [15:0] Sum,
  output Overflow
);

  wire carry_logic_1_c1, carry_logic_1_c2, carry_logic_1_c3, carry_logic_1_c4, n4_bit_adder_1_g,
       n4_bit_adder_1_p, n4_bit_adder_2_g, n4_bit_adder_2_p, n4_bit_adder_3_g, n4_bit_adder_3_p,
       n4_bit_adder_4_g, n4_bit_adder_4_p;

  _4_bit_Adder u_4_bit_adder_1 (
    .A(A[3:0]), .B(B[3:0]), .CarryIn(C_in), .P(n4_bit_adder_1_p), .G(n4_bit_adder_1_g), .out_6(Sum[3:0]));
  _4_bit_Adder u_4_bit_adder_2 (
    .A(A[7:4]), .B(B[7:4]), .CarryIn(carry_logic_1_c1), .P(n4_bit_adder_2_p), .G(n4_bit_adder_2_g),
    .out_6(Sum[7:4]));
  _4_bit_Adder u_4_bit_adder_3 (
    .A(A[11:8]), .B(B[11:8]), .CarryIn(carry_logic_1_c2), .P(n4_bit_adder_3_p), .G(n4_bit_adder_3_g),
    .out_6(Sum[11:8]));
  _4_bit_Adder u_4_bit_adder_4 (
    .A(A[15:12]), .B(B[15:12]), .CarryIn(carry_logic_1_c3), .P(n4_bit_adder_4_p), .G(n4_bit_adder_4_g),
    .out_6(Sum[15:12]));
  xor xor_1 (Overflow, carry_logic_1_c4, carry_logic_1_c3);
  Carry_Logic carry_logic_1 (
    .g0(n4_bit_adder_1_g), .g1(n4_bit_adder_2_g), .g2(n4_bit_adder_3_g), .g3(n4_bit_adder_4_g),
    .p0(n4_bit_adder_1_p), .p1(n4_bit_adder_2_p), .p2(n4_bit_adder_3_p), .p3(n4_bit_adder_4_p), .c0(C_in),
    .c1(carry_logic_1_c1), .c2(carry_logic_1_c2), .c3(carry_logic_1_c3), .c4(carry_logic_1_c4));
endmodule

module test1 (
  input  [15:0] A,
  input  [15:0] B,
  input  in_3,
  output [15:0] out_4,
  output [15:0] out_5,
  output out_6,
  output out_7
);

  _16_Bit_Carry_Lookahead_Adder u_16_bit_carry_lookahead_adder_1 (
    .A(A), .B(B), .C_in(in_3), .Sum(out_4), .Overflow(out_7));
  _16_bit_ripple_carry_adder__2_s_complement u_16_bit_ripple_carry_adder_2_s_complement_1 (
    .overflow(out_6), .a(A), .b(B), .CarryIn(in_3), .out_4(out_5));
endmodule
