// Logisim project ALU_Group01.circ as structural Verilog: 10 circuits, main circuit main
module main (
  output halt,
  output [8:0] counter,
  output [3:0] op,
  output [15:0] a,
  output [15:0] b,
  output [15:0] oracle,
  output [15:0] result,
  output err_oracle,
  output error,
  output ok,
  output start_delimiter
);

  wire and_1_out, and_2_out, clock_1_out, comparator_1_eq, comparator_2_eq;

  Clock clock_1 (.out(clock_1_out));
  Counter #(.width(9), .max('h1ff), .trigger("falling")) counter_1 (
    .Q(counter), .carry(halt), .clk(clock_1_out));  // open: load, D, count, clr
  RAM #(.addrWidth(12), .dataWidth(4), .bus("separate")) ram_1 (
    .addr({counter, 3'b000}), .data(op), .ld(1'b1));  // open: din, str, sel, clk, clr
  RAM #(.addrWidth(12), .dataWidth(16), .bus("separate")) ram_2 (
    .addr({counter, 3'b001}), .data(a), .ld(1'b1));  // open: din, str, sel, clk, clr
  RAM #(.addrWidth(12), .dataWidth(16), .bus("separate")) ram_3 (
    .addr({counter, 3'b010}), .data(b), .ld(1'b1));  // open: din, str, sel, clk, clr
  RAM #(.addrWidth(12), .dataWidth(16), .bus("separate")) ram_4 (
    .addr({counter, 3'b011}), .data(oracle), .ld(1'b1));  // open: din, str, sel, clk, clr
  RAM #(.addrWidth(12), .dataWidth(1), .bus("separate")) ram_5 (
    .addr({counter, 3'b100}), .data(err_oracle), .ld(1'b1));  // open: din, str, sel, clk, clr
  RAM #(.addrWidth(12), .dataWidth(1), .bus("separate")) ram_6 (
    .addr({counter, 3'b101}), .data(start_delimiter), .ld(1'b1));  // open: din, str, sel, clk, clr
  _16_bit_ALU u_16_bit_alu_1 (.ALU_code(op), .a(a), .b(b), .overflow(error), .result(result));
  Comparator #(.width(1), .mode("unsigned")) comparator_1 (
    .a(error), .b(err_oracle), .eq(comparator_1_eq));  // open: gt, lt
  Comparator #(.width(16)) comparator_2 (.a(result), .b(oracle), .eq(comparator_2_eq));  // open: gt, lt
  and and_1 (and_1_out, comparator_1_eq, error);
  and and_2 (and_2_out, comparator_2_eq, comparator_1_eq, ~error);  // AND_Gate
  or or_1 (ok, and_1_out, and_2_out);

  // Notes on the sheet:
  //   You must complete the circuit '12-bit ALU' instead.
  //   DO NOT EDIT THIS CIRCUIT!
endmodule

module _16_bit_ALU (
  input  [3:0] ALU_code,
  input  [15:0] a,
  input  [15:0] b,
  output [15:0] result,
  output overflow
);

  wire alu_operation_logic_1_a_invert, alu_operation_logic_1_b_invert, alu_operation_logic_1_enable_eq_test,
       alu_operation_logic_1_enable_num_inverse, alu_operation_logic_1_enable_shift,
       alu_operation_logic_1_eq_ne, alu_operation_logic_1_left_right,
       alu_operation_logic_1_logical_arithmetic, alu_operation_logic_1_overflow_disable;
  wire [3:0] alu_operation_logic_1_operation_2;

  _16_Bit_ALU u_16_bit_alu_1 (
    .A(a), .B(b), .A_invert(alu_operation_logic_1_a_invert), .B_invert(alu_operation_logic_1_b_invert),
    .Operation(alu_operation_logic_1_operation_2), .Output(result), .Overflow(overflow),
    .enable_num_inverse(alu_operation_logic_1_enable_num_inverse), .eq_neq(alu_operation_logic_1_eq_ne),
    .enable_eq_test(alu_operation_logic_1_enable_eq_test), .left_right(alu_operation_logic_1_left_right),
    .logic_arithmetic(alu_operation_logic_1_logical_arithmetic),
    .enable_shift(alu_operation_logic_1_enable_shift),
    .overflow_disable(alu_operation_logic_1_overflow_disable));
  ALU_Operation_Logic alu_operation_logic_1 (
    .operation_2(alu_operation_logic_1_operation_2), .Operation(ALU_code),
    .A_invert(alu_operation_logic_1_a_invert), .B_invert(alu_operation_logic_1_b_invert),
    .eq_ne(alu_operation_logic_1_eq_ne), .enable_eq_test(alu_operation_logic_1_enable_eq_test),
    .enable_num_inverse(alu_operation_logic_1_enable_num_inverse),
    .enable_shift(alu_operation_logic_1_enable_shift),
    .logical_arithmetic(alu_operation_logic_1_logical_arithmetic),
    .left_right(alu_operation_logic_1_left_right), .overflow_disable(alu_operation_logic_1_overflow_disable));

  // Notes on the sheet:
  //   This circuit is used as a block in the main circuit, and its layout must remain unchanged. The circuit called "main" should be the main circuit of this file.
  //   Do not change the circuit appearance.
  //   DO NOT CHANGE THE INPUTS AND OUTPUTS OF THIS CIRCUIT!
  //   Do not add/remove inputs or outputs. Do not even change their location or orientation.
endmodule

module _1_Bit_Full_Adder (
  input  a,
  input  b,
  input  CarryIn,
  output CarryOut,
  output Sum,
  output Generate,
  output Propagate
);

  wire and_1_out, and_2_out, and_3_out, and_4_out, and_5_out, and_6_out, and_7_out, not_1_out, not_2_out,
       not_3_out, not_4_out, not_5_out, not_6_out;

  and and_1 (and_1_out, b, CarryIn);
  and and_2 (and_2_out, a, CarryIn);
  and and_3 (and_3_out, a, b);
  not not_1 (not_1_out, a);
  not not_2 (not_2_out, b);
  not not_3 (not_3_out, a);
  not not_4 (not_4_out, CarryIn);
  not not_5 (not_5_out, b);
  not not_6 (not_6_out, CarryIn);
  or or_1 (CarryOut, and_1_out, and_2_out, and_3_out);
  and and_4 (and_4_out, not_1_out, not_2_out, CarryIn);
  and and_5 (and_5_out, not_3_out, b, not_4_out);
  and and_6 (and_6_out, a, not_5_out, not_6_out);
  and and_7 (and_7_out, a, b, CarryIn);
  and and_8 (Generate, a, b);
  or or_2 (Propagate, a, b);
  or or_3 (Sum, and_4_out, and_5_out, and_6_out, and_7_out);
endmodule

module Carry_Logic (
  input  g0,
  input  g1,
  input  g2,
  input  g3,
  input  p0,
  input  p1,
  input  p2,
  input  p3,
  input  c0,
  output c1,
  output c2,
  output c3,
  output c4,
  output P,
  output G
);

  wire and_1_out, and_2_out, and_3_out, and_4_out, and_5_out, and_6_out, and_7_out, and_8_out, and_9_out,
       and_10_out, and_11_out, and_12_out, and_13_out;

  and and_1 (and_1_out, g0, p3, p2, p1);
  and and_2 (and_2_out, g1, p3, p2);
  and and_3 (and_3_out, g2, p3);
  and and_4 (and_4_out, p0, c0);
  and and_5 (and_5_out, p1, g0);
  and and_6 (and_6_out, p0, p1, c0);
  and and_7 (and_7_out, p2, g1);
  and and_8 (and_8_out, p2, p1, g0);
  and and_9 (and_9_out, p2, p1, p0, c0);
  and and_10 (and_10_out, p3, g2);
  and and_11 (and_11_out, p3, p2, g1);
  and and_12 (and_12_out, p3, p2, p1, g0);
  and and_13 (and_13_out, p3, p2, p1, p0, c0);
  or or_1 (c1, g0, and_4_out);
  or or_2 (c2, g1, and_5_out, and_6_out);
  or or_3 (c3, g2, and_7_out, and_8_out, and_9_out);
  or or_4 (c4, g3, and_10_out, and_11_out, and_12_out, and_13_out);
  and and_14 (P, p0, p1, p2, p3);
  or or_5 (G, g3, and_1_out, and_2_out, and_3_out);
endmodule

module _1_Bit_ALU (
  input  [3:0] Operation,
  input  cin,
  input  less,
  input  A_invert,
  input  B_invert,
  input  a,
  input  b,
  output result,
  output G,
  output P,
  output Set,
  output overflow
);

  wire and_1_out, multiplexer_1_out, multiplexer_2_out, n1_bit_full_adder_1_carryout,
       n1_bit_full_adder_1_sum, not_1_out, not_2_out, not_3_out, or_1_out;

  Multiplexer multiplexer_1 (.in0(a), .in1(not_1_out), .out(multiplexer_1_out), .sel(A_invert));  // open: en
  not not_1 (not_1_out, a);
  not not_2 (not_2_out, b);
  Multiplexer multiplexer_2 (.in0(b), .in1(not_2_out), .out(multiplexer_2_out), .sel(B_invert));  // open: en
  and and_1 (and_1_out, multiplexer_1_out, multiplexer_2_out);
  or or_1 (or_1_out, multiplexer_1_out, multiplexer_2_out);
  _1_Bit_Full_Adder u_1_bit_full_adder_1 (
    .a(multiplexer_1_out), .b(multiplexer_2_out), .CarryIn(cin), .CarryOut(n1_bit_full_adder_1_carryout),
    .Sum(n1_bit_full_adder_1_sum), .Generate(G), .Propagate(P));
  not not_3 (not_3_out, a);
  xor xor_1 (overflow, cin, n1_bit_full_adder_1_carryout);
  xor xor_2 (Set, n1_bit_full_adder_1_sum, overflow);
  Multiplexer #(.select(4), .enable("false")) multiplexer_3 (
    .in0(1'b0), .in1(not_3_out), .in2(and_1_out), .in3(or_1_out), .in4(n1_bit_full_adder_1_sum),
    .in5(n1_bit_full_adder_1_sum), .in6(less), .in7(less), .in8(n1_bit_full_adder_1_sum),
    .in9(n1_bit_full_adder_1_sum), .in10(n1_bit_full_adder_1_sum), .in11(a), .in12(a), .in13(a), .in14(a),
    .in15(a), .out(result), .sel(Operation));

  // Notes on the sheet:
  //   overflow
  //   sign
endmodule

module _4_Bit_ALU (
  input  [3:0] A,
  input  [3:0] B,
  input  A_invert,
  input  B_invert,
  input  CarryIn,
  input  Less,
  input  [3:0] Operation,
  output overflow,
  output Set,
  output G,
  output P,
  output [3:0] Sum
);

  wire carry_logic_1_c1, carry_logic_1_c2, carry_logic_1_c3, n1_bit_alu_1_g, n1_bit_alu_1_p, n1_bit_alu_2_g,
       n1_bit_alu_2_p, n1_bit_alu_3_g, n1_bit_alu_3_p, n1_bit_alu_4_g, n1_bit_alu_4_p;

  _1_Bit_ALU u_1_bit_alu_1 (
    .a(A[0]), .b(B[0]), .result(Sum[0]), .A_invert(A_invert), .B_invert(B_invert), .cin(CarryIn),
    .less(Less), .Operation(Operation), .G(n1_bit_alu_1_g), .P(n1_bit_alu_1_p));  // open: Set, overflow
  _1_Bit_ALU u_1_bit_alu_2 (
    .a(A[1]), .b(B[1]), .result(Sum[1]), .A_invert(A_invert), .B_invert(B_invert), .cin(carry_logic_1_c1),
    .less(1'b0), .Operation(Operation), .G(n1_bit_alu_2_g), .P(n1_bit_alu_2_p));  // open: Set, overflow
  _1_Bit_ALU u_1_bit_alu_3 (
    .a(A[2]), .b(B[2]), .result(Sum[2]), .A_invert(A_invert), .B_invert(B_invert), .cin(carry_logic_1_c2),
    .less(1'b0), .Operation(Operation), .G(n1_bit_alu_3_g), .P(n1_bit_alu_3_p));  // open: Set, overflow
  _1_Bit_ALU u_1_bit_alu_4 (
    .a(A[3]), .b(B[3]), .result(Sum[3]), .Set(Set), .A_invert(A_invert), .B_invert(B_invert),
    .cin(carry_logic_1_c3), .less(1'b0), .Operation(Operation), .G(n1_bit_alu_4_g), .P(n1_bit_alu_4_p),
    .overflow(overflow));
  Carry_Logic carry_logic_1 (
    .g0(n1_bit_alu_1_g), .g1(n1_bit_alu_2_g), .g2(n1_bit_alu_3_g), .g3(n1_bit_alu_4_g), .p0(n1_bit_alu_1_p),
    .p1(n1_bit_alu_2_p), .p2(n1_bit_alu_3_p), .p3(n1_bit_alu_4_p), .c0(CarryIn), .c1(carry_logic_1_c1),
    .c2(carry_logic_1_c2), .c3(carry_logic_1_c3), .P(P), .G(G));  // open: c4
endmodule

module _16_Bit_ALU (
  input  enable_num_inverse,
  input  [15:0] A,
  input  [15:0] B,
  input  A_invert,
  input  B_invert,
  input  [3:0] Operation,
  input  overflow_disable,
  input  enable_shift,
  input  logic_arithmetic,
  input  left_right,
  input  enable_eq_test,
  input  eq_neq,
  output [15:0] Output,
  output Overflow
);

  wire carry_logic_1_c1, carry_logic_1_c2, carry_logic_1_c3, logical_shift_1_overflow, multiplexer_4_out,
       n4_bit_alu_1_g, n4_bit_alu_1_p, n4_bit_alu_2_g, n4_bit_alu_2_p, n4_bit_alu_3_g, n4_bit_alu_3_p,
       n4_bit_alu_4_g, n4_bit_alu_4_overflow, n4_bit_alu_4_p, n4_bit_alu_4_set, or_1_out;
  wire [3:0] n4_bit_alu_1_sum, n4_bit_alu_2_sum, n4_bit_alu_3_sum, n4_bit_alu_4_sum;
  wire [15:0] eq_ne_test_1_output, logical_shift_1_out_5, multiplexer_1_out, multiplexer_2_out;

  Multiplexer #(.width(16), .enable("false")) multiplexer_1 (
    .in0(B), .in1({16{1'b0}}), .out(multiplexer_1_out), .sel(enable_num_inverse));
  or or_1 (or_1_out, B_invert, A_invert);
  _4_Bit_ALU u_4_bit_alu_1 (
    .A(A[3:0]), .B(multiplexer_1_out[3:0]), .A_invert(A_invert), .B_invert(B_invert),
    .Less(n4_bit_alu_4_set), .Operation(Operation), .Sum(n4_bit_alu_1_sum), .G(n4_bit_alu_1_g),
    .P(n4_bit_alu_1_p), .CarryIn(or_1_out));  // open: Set, overflow
  _4_Bit_ALU u_4_bit_alu_2 (
    .A(A[7:4]), .B(multiplexer_1_out[7:4]), .A_invert(A_invert), .B_invert(B_invert), .Less(1'b0),
    .Operation(Operation), .Sum(n4_bit_alu_2_sum), .G(n4_bit_alu_2_g), .P(n4_bit_alu_2_p),
    .CarryIn(carry_logic_1_c1));  // open: Set, overflow
  _4_Bit_ALU u_4_bit_alu_3 (
    .A(A[11:8]), .B(multiplexer_1_out[11:8]), .A_invert(A_invert), .B_invert(B_invert), .Less(1'b0),
    .Operation(Operation), .Sum(n4_bit_alu_3_sum), .G(n4_bit_alu_3_g), .P(n4_bit_alu_3_p),
    .CarryIn(carry_logic_1_c2));  // open: Set, overflow
  _4_Bit_ALU u_4_bit_alu_4 (
    .A(A[15:12]), .B(multiplexer_1_out[15:12]), .A_invert(A_invert), .B_invert(B_invert), .Less(1'b0),
    .Operation(Operation), .Set(n4_bit_alu_4_set), .Sum(n4_bit_alu_4_sum), .G(n4_bit_alu_4_g),
    .P(n4_bit_alu_4_p), .CarryIn(carry_logic_1_c3), .overflow(n4_bit_alu_4_overflow));
  Carry_Logic carry_logic_1 (
    .g0(n4_bit_alu_1_g), .g1(n4_bit_alu_2_g), .g2(n4_bit_alu_3_g), .g3(n4_bit_alu_4_g), .p0(n4_bit_alu_1_p),
    .p1(n4_bit_alu_2_p), .p2(n4_bit_alu_3_p), .p3(n4_bit_alu_4_p), .c0(or_1_out), .c1(carry_logic_1_c1),
    .c2(carry_logic_1_c2), .c3(carry_logic_1_c3));  // open: c4, P, G
  eq_ne_Test eq_ne_test_1 (
    .\output (eq_ne_test_1_output), .eq_ne(eq_neq),
    .\input ({n4_bit_alu_4_sum, n4_bit_alu_3_sum, n4_bit_alu_2_sum, n4_bit_alu_1_sum}));
  Multiplexer #(.width(16), .enable("false")) multiplexer_2 (
    .in0({n4_bit_alu_4_sum, n4_bit_alu_3_sum, n4_bit_alu_2_sum, n4_bit_alu_1_sum}),
    .in1(eq_ne_test_1_output), .out(multiplexer_2_out), .sel(enable_eq_test));
  Logical_Shift logical_shift_1 (
    .logic_arithmetic(logic_arithmetic), .\input (multiplexer_2_out), .left_right(left_right),
    .overflow(logical_shift_1_overflow), .out_5(logical_shift_1_out_5));
  Multiplexer #(.width(16), .enable("false")) multiplexer_3 (
    .in0(multiplexer_2_out), .in1(logical_shift_1_out_5), .out(Output), .sel(enable_shift));
  Multiplexer #(.enable("false")) multiplexer_4 (
    .in0(n4_bit_alu_4_overflow), .in1(logical_shift_1_overflow), .out(multiplexer_4_out), .sel(enable_shift));
  Multiplexer #(.enable("false")) multiplexer_5 (
    .in0(multiplexer_4_out), .in1(1'b0), .out(Overflow), .sel(overflow_disable));
endmodule

module ALU_Operation_Logic (
  input  [3:0] Operation,
  output [3:0] operation_2,
  output A_invert,
  output B_invert,
  output eq_ne,
  output enable_eq_test,
  output enable_num_inverse,
  output enable_shift,
  output logical_arithmetic,
  output left_right,
  output overflow_disable
);

  wire decoder_1_out0, decoder_1_out1, decoder_1_out2, decoder_1_out3, decoder_1_out5, decoder_1_out6,
       decoder_1_out7, decoder_1_out9, decoder_1_out11, decoder_1_out12, decoder_1_out13, decoder_1_out14,
       decoder_1_out15;

  or or_1 (A_invert, decoder_1_out7, enable_num_inverse);
  Decoder #(.select(4), .enable("false")) decoder_1 (
    .out0(decoder_1_out0), .out1(decoder_1_out1), .out2(decoder_1_out2), .out3(decoder_1_out3),
    .out5(decoder_1_out5), .out6(decoder_1_out6), .out7(decoder_1_out7), .out8(eq_ne), .out9(decoder_1_out9),
    .out10(enable_num_inverse), .out11(decoder_1_out11), .out12(decoder_1_out12), .out13(decoder_1_out13),
    .out14(decoder_1_out14), .out15(decoder_1_out15), .sel(Operation));  // open: out4
  or or_2 (B_invert, decoder_1_out5, decoder_1_out6, eq_ne, decoder_1_out9);
  or or_3 (enable_eq_test, eq_ne, decoder_1_out9);
  or or_4 (enable_shift, decoder_1_out11, decoder_1_out12, decoder_1_out13, decoder_1_out14);
  or or_5 (logical_arithmetic, decoder_1_out13, decoder_1_out14);
  or or_6 (left_right, decoder_1_out12, decoder_1_out14);
  or or_7 (overflow_disable, decoder_1_out0, decoder_1_out1, decoder_1_out2, decoder_1_out3, decoder_1_out6, decoder_1_out7, eq_ne, decoder_1_out9, decoder_1_out11, decoder_1_out12, decoder_1_out14, decoder_1_out15);

  assign operation_2 = Operation;
endmodule

module eq_ne_Test (
  input  [15:0] \input ,
  input  eq_ne,
  output [15:0] \output 
);

  wire not_1_out, not_2_out, or_1_out;

  Multiplexer multiplexer_1 (.in0(not_1_out), .in1(not_2_out), .out(\output [0]), .sel(eq_ne));  // open: en
  not not_1 (not_1_out, not_2_out);
  or or_1 (or_1_out, \input [15], \input [14], \input [13], \input [12], \input [11], \input [10], \input [9], \input [8], \input [7], \input [6], \input [5], \input [4], \input [3], \input [2], \input [1], \input [0]);
  not not_2 (not_2_out, or_1_out);

  assign \output [15:1] = {15{1'b0}};
endmodule

module Logical_Shift (
  input  [15:0] \input ,
  input  left_right,
  input  logic_arithmetic,
  output overflow,
  output [15:0] out_5
);

  wire [15:0] multiplexer_1_out, multiplexer_3_out;
  wire [15:15] and_1_out;

  Multiplexer #(.width(16)) multiplexer_1 (
    .in0({\input [14:0], 1'b0}), .in1({1'b0, \input [15:1]}), .out(multiplexer_1_out), .sel(left_right));  // open: en
  xor xor_1 (overflow, \input [15], \input [14]);
  Multiplexer #(.width(16)) multiplexer_2 (
    .in0(multiplexer_1_out), .in1(multiplexer_3_out), .out(out_5), .sel(logic_arithmetic));  // open: en
  and and_1 (and_1_out[15], 1'b1, \input [15]);
  Multiplexer #(.width(16)) multiplexer_3 (
    .in0({\input [14:0], 1'b0}), .in1({and_1_out[15], \input [15:1]}), .out(multiplexer_3_out),
    .sel(left_right));  // open: en
endmodule
