// Logisim project FD_Group01.circ as structural Verilog: 8 circuits, main circuit main
module main (
  output [15:0] pc,
  output [15:0] r0,
  output [15:0] r1,
  output [15:0] r2,
  output [15:0] r3,
  output [15:0] r4,
  output [15:0] r5,
  output [15:0] r6,
  output [15:0] r7,
  output halt
);

  wire clk, clock_1_out, control_unit_1_branch, control_unit_1_jump, hazard_detection_unit_1_exception,
       ImmOp, inc_dec, lui, MemOp, n16_bit_alu_1_overflow, or_1_out, RegWrite, rst, sw;
  wire [2:0] control_unit_1_rd, control_unit_1_rs, control_unit_1_rt;
  wire [3:0] ALU_Code;
  wire [15:0] control_unit_1_branch_value, immediate, multiplexer_1_out, multiplexer_2_out,
       multiplexer_3_out, multiplexer_4_out, n16_bit_alu_1_result, ram_1_data, ram_2_data,
       register_file_1_out_8, register_file_1_out_9;

  Halt halt_1 (
    .instruction(ram_1_data), .exception(hazard_detection_unit_1_exception), .halt(halt),
    .clock(clock_1_out), .reset(rst));
  Clock clock_1 (.out(clock_1_out));
  Button reset (.out(rst));
  and and_1 (clk, ~halt, clock_1_out);  // AND_Gate
  PC pc_1 (
    .Branch__Value(control_unit_1_branch_value), .Reset(rst), .Instruction_Address(pc),
    .Branch_Relative(control_unit_1_branch), .Branch_Absolute(control_unit_1_jump), .Clock(clk));
  Hazard_Detection_Unit hazard_detection_unit_1 (
    .instruction(ram_1_data), .exception(hazard_detection_unit_1_exception), .overflow(n16_bit_alu_1_overflow));
  RAM #(.addrWidth(16), .dataWidth(16), .bus("asynch")) ram_1 (.addr(pc), .data(ram_1_data));  // open: sel, ld, clr
  Control_Unit control_unit_1 (
    .instruction(ram_1_data), .ALU_code(ALU_Code), .rd(control_unit_1_rd), .rs(control_unit_1_rs),
    .rt(control_unit_1_rt), .lw_sw(sw), .MemOp(MemOp), .immediate(immediate), .inc_dec(inc_dec),
    .Branch_Value(control_unit_1_branch_value), .ImmOp(ImmOp), .reg_write(RegWrite),
    .ALU_output(n16_bit_alu_1_result), .PC(pc), .jump(control_unit_1_jump), .branch(control_unit_1_branch),
    .lui(lui));
  Register_File register_file_1 (
    .Data(multiplexer_4_out), .write(RegWrite), .rd(control_unit_1_rd), .reset(rst), .clock(clk),
    .rs(control_unit_1_rs), .out_8(register_file_1_out_8), .rt(control_unit_1_rt),
    .out_9(register_file_1_out_9), .r0(r0), .r1(r1), .r2(r2), .r3(r3), .r4(r4), .r5(r5), .r6(r6), .r7(r7));
  or or_1 (or_1_out, MemOp, ImmOp);
  Multiplexer #(.width(16), .enable("false")) multiplexer_1 (
    .in0(register_file_1_out_9), .in1(immediate), .out(multiplexer_1_out), .sel(or_1_out));
  Multiplexer #(.width(16), .enable("false")) multiplexer_2 (
    .in0(register_file_1_out_8), .in1({immediate[7:0], {8{1'b0}}}), .out(multiplexer_2_out), .sel(lui));
  Multiplexer #(.width(16), .enable("false")) multiplexer_3 (
    .in0(multiplexer_1_out), .in1(16'h1), .out(multiplexer_3_out), .sel(inc_dec));
  _16_bit_ALU u_16_bit_alu_1 (
    .ALU_code(ALU_Code), .a(multiplexer_2_out), .b(multiplexer_3_out), .overflow(n16_bit_alu_1_overflow),
    .result(n16_bit_alu_1_result));
  Multiplexer #(.width(16), .enable("false")) multiplexer_4 (
    .in0(n16_bit_alu_1_result), .in1(ram_2_data), .out(multiplexer_4_out), .sel(MemOp));
  RAM #(.addrWidth(16), .dataWidth(16), .bus("separate")) ram_2 (
    .addr(n16_bit_alu_1_result), .din(register_file_1_out_9), .data(ram_2_data), .str(sw), .clk(clk),
    .ld(1'b1));  // open: sel, clr

  // Notes on the sheet:
  //   current instruction
  //   clock signal
  //   reset button
  //   DO NOT CHANGE THE INPUTS AND OUTPUTS OF THIS CIRCUIT! Do not add/remove inputs or outputs. Do not even change their location or orientation.
endmodule

module Halt (
  input  [15:0] instruction,
  input  exception,
  input  clock,
  input  reset,
  output halt
);

  wire and_1_out, comparator_1_eq, comparator_2_gt, counter_1_carry, or_1_out, or_2_out, register_1_q;
  wire [11:0] counter_1_q;

  Comparator #(.width(16), .mode("unsigned")) comparator_1 (
    .a(instruction), .b({16{1'b0}}), .eq(comparator_1_eq));  // open: gt, lt
  Counter #(.width(12), .max('hfff), .trigger("falling")) counter_1 (
    .Q(counter_1_q), .carry(counter_1_carry), .clk(clock), .clr(reset));  // open: load, D, count
  or or_1 (or_1_out, comparator_1_eq, counter_1_carry);
  Comparator #(.width(12), .mode("unsigned")) comparator_2 (
    .a(counter_1_q), .b({12{1'b0}}), .gt(comparator_2_gt));  // open: eq, lt
  or or_2 (or_2_out, register_1_q, and_1_out);
  and and_1 (and_1_out, or_1_out, comparator_2_gt);
  Register_part #(.width(1)) register_1 (.D(or_2_out), .Q(register_1_q), .clk(clock), .clr(reset));  // open: en
  or or_3 (halt, exception, register_1_q);

  // Notes on the sheet:
  //   halt becomes and stays asserted if the instruction is 0000 (not in the first clock cycle) or the end of the counter is reached (2^12)
endmodule

module Register (
  input  reset,
  input  write,
  input  clock,
  input  [15:0] D,
  output [15:0] Q
);

  D_Flip_Flop #(.trigger("falling")) d_ff_1 (
    .clk(clock), .D(D[0]), .Q(Q[0]), .en(write), .reset(reset));  // open: Qn, preset
  D_Flip_Flop #(.trigger("falling")) d_ff_2 (
    .clk(clock), .D(D[1]), .Q(Q[1]), .en(write), .reset(reset));  // open: Qn, preset
  D_Flip_Flop #(.trigger("falling")) d_ff_3 (
    .clk(clock), .D(D[2]), .Q(Q[2]), .en(write), .reset(reset));  // open: Qn, preset
  D_Flip_Flop #(.trigger("falling")) d_ff_4 (
    .clk(clock), .D(D[3]), .Q(Q[3]), .en(write), .reset(reset));  // open: Qn, preset
  D_Flip_Flop #(.trigger("falling")) d_ff_5 (
    .clk(clock), .D(D[4]), .Q(Q[4]), .en(write), .reset(reset));  // open: Qn, preset
  D_Flip_Flop #(.trigger("falling")) d_ff_6 (
    .clk(clock), .D(D[5]), .Q(Q[5]), .en(write), .reset(reset));  // open: Qn, preset
  D_Flip_Flop #(.trigger("falling")) d_ff_7 (
    .clk(clock), .D(D[6]), .Q(Q[6]), .en(write), .reset(reset));  // open: Qn, preset
  D_Flip_Flop #(.trigger("falling")) d_ff_8 (
    .clk(clock), .D(D[7]), .Q(Q[7]), .en(write), .reset(reset));  // open: Qn, preset
  D_Flip_Flop #(.trigger("falling")) d_ff_9 (
    .clk(clock), .D(D[8]), .Q(Q[8]), .en(write), .reset(reset));  // open: Qn, preset
  D_Flip_Flop #(.trigger("falling")) d_ff_10 (
    .clk(clock), .D(D[9]), .Q(Q[9]), .en(write), .reset(reset));  // open: Qn, preset
  D_Flip_Flop #(.trigger("falling")) d_ff_11 (
    .clk(clock), .D(D[10]), .Q(Q[10]), .en(write), .reset(reset));  // open: Qn, preset
  D_Flip_Flop #(.trigger("falling")) d_ff_12 (
    .clk(clock), .D(D[11]), .Q(Q[11]), .en(write), .reset(reset));  // open: Qn, preset
  D_Flip_Flop #(.trigger("falling")) d_ff_13 (
    .clk(clock), .D(D[12]), .Q(Q[12]), .en(write), .reset(reset));  // open: Qn, preset
  D_Flip_Flop #(.trigger("falling")) d_ff_14 (
    .clk(clock), .D(D[13]), .Q(Q[13]), .en(write), .reset(reset));  // open: Qn, preset
  D_Flip_Flop #(.trigger("falling")) d_ff_15 (
    .clk(clock), .D(D[14]), .Q(Q[14]), .en(write), .reset(reset));  // open: Qn, preset
  D_Flip_Flop #(.trigger("falling")) d_ff_16 (
    .clk(clock), .D(D[15]), .Q(Q[15]), .en(write), .reset(reset));  // open: Qn, preset
endmodule

module PC (
  input  Branch_Relative,
  input  Branch_Absolute,
  input  Clock,
  input  [15:0] Branch__Value,
  input  Reset,
  output [15:0] Instruction_Address
);

  wire and_1_out, nand_1_out, not_1_out, not_2_out, or_1_out;
  wire [15:0] adder_1_out, multiplexer_1_out, multiplexer_2_out;

  Multiplexer #(.width(16), .enable("false")) multiplexer_1 (
    .in0({16{1'b0}}), .in1(Branch__Value), .out(multiplexer_1_out), .sel(Branch_Relative));
  not not_1 (not_1_out, Branch_Absolute);
  not not_2 (not_2_out, Branch_Relative);
  and and_1 (and_1_out, not_2_out, not_1_out);
  or or_1 (or_1_out, Branch_Relative, and_1_out);
  Adder #(.width(16)) adder_1 (
    .a(multiplexer_1_out), .b(Instruction_Address), .out(adder_1_out), .cin(or_1_out));  // open: cout
  Multiplexer #(.width(16), .enable("false")) multiplexer_2 (
    .in0(adder_1_out), .in1(Branch__Value), .out(multiplexer_2_out), .sel(Branch_Absolute));
  nand nand_1 (nand_1_out, Branch_Relative, Branch_Absolute);
  Register register_1 (
    .D(multiplexer_2_out), .reset(Reset), .write(nand_1_out), .clock(Clock), .Q(Instruction_Address));
endmodule

module Register_File (
  input  write,
  input  [2:0] rd,
  input  reset,
  input  clock,
  input  [2:0] rs,
  input  [2:0] rt,
  input  [15:0] Data,
  output [15:0] out_8,
  output [15:0] out_9,
  output [15:0] r0,
  output [15:0] r1,
  output [15:0] r2,
  output [15:0] r3,
  output [15:0] r4,
  output [15:0] r5,
  output [15:0] r6,
  output [15:0] r7
);

  wire demultiplexer_1_out1, demultiplexer_1_out2, demultiplexer_1_out3, demultiplexer_1_out4,
       demultiplexer_1_out5, demultiplexer_1_out6, demultiplexer_1_out7;

  Demultiplexer #(.select(3), .enable("false")) demultiplexer_1 (
    .out1(demultiplexer_1_out1), .out2(demultiplexer_1_out2), .out3(demultiplexer_1_out3),
    .out4(demultiplexer_1_out4), .out5(demultiplexer_1_out5), .out6(demultiplexer_1_out6),
    .out7(demultiplexer_1_out7), .in(write), .sel(rd));  // open: out0
  Register register_1 (.D(Data), .reset(reset), .write(demultiplexer_1_out1), .clock(clock), .Q(r1));
  Register register_2 (.D(Data), .reset(reset), .write(demultiplexer_1_out2), .clock(clock), .Q(r2));
  Register register_3 (.D(Data), .reset(reset), .write(demultiplexer_1_out3), .clock(clock), .Q(r3));
  Register register_4 (.D(Data), .reset(reset), .write(demultiplexer_1_out4), .clock(clock), .Q(r4));
  Register register_5 (.D(Data), .reset(reset), .write(demultiplexer_1_out5), .clock(clock), .Q(r5));
  Register register_6 (.D(Data), .reset(reset), .write(demultiplexer_1_out6), .clock(clock), .Q(r6));
  Register register_7 (.D(Data), .reset(reset), .write(demultiplexer_1_out7), .clock(clock), .Q(r7));
  Multiplexer #(.select(3), .width(16), .enable("false")) multiplexer_1 (
    .in0({16{1'b0}}), .in1(r1), .in2(r2), .in3(r3), .in4(r4), .in5(r5), .in6(r6), .in7(r7), .out(out_8),
    .sel(rs));
  Multiplexer #(.select(3), .width(16), .enable("false")) multiplexer_2 (
    .in0({16{1'b0}}), .in1(r1), .in2(r2), .in3(r3), .in4(r4), .in5(r5), .in6(r6), .in7(r7), .out(out_9),
    .sel(rt));

  assign r0 = {16{1'b0}};
endmodule

module Control_Unit (
  input  [15:0] instruction,
  input  [15:0] ALU_output,
  input  [15:0] PC,
  output MemOp,
  output ImmOp,
  output reg_write,
  output lui,
  output jump,
  output [15:0] Branch_Value,
  output branch,
  output [3:0] ALU_code,
  output [2:0] rd,
  output [2:0] rs,
  output [2:0] rt,
  output lw_sw,
  output [15:0] immediate,
  output inc_dec
);

  wire and_2_out, and_3_out, and_4_out, check, comparator_1_eq, comparator_2_eq, not_1_out, not_2_out,
       not_3_out, not_4_out, not_5_out, or_2_out;
  wire [3:0] multiplexer_1_out, multiplexer_2_out;
  wire [15:0] adder_1_out, bit_extender_1_out, jrImm, signed_imm, unsigned_imm;

  Multiplexer #(.select(2), .width(4), .enable("false")) multiplexer_1 (
    .in0(4'b0011), .in1(4'b1111), .in2(4'b0100), .in3(4'b0101), .out(multiplexer_1_out),
    .sel(instruction[12:11]));
  Multiplexer #(.width(4), .enable("false")) multiplexer_2 (
    .in0(4'b1000), .in1(4'b0111), .out(multiplexer_2_out), .sel(instruction[12]));
  not not_1 (not_1_out, instruction[15]);
  and and_1 (check, not_1_out, not_2_out);
  not not_2 (not_2_out, instruction[14]);
  and and_2 (and_2_out, instruction[15], instruction[14], not_3_out);
  not not_3 (not_3_out, instruction[13]);
  and and_3 (and_3_out, instruction[15], instruction[14], instruction[13]);
  not not_4 (not_4_out, instruction[14]);
  and and_4 (and_4_out, instruction[15], not_4_out, instruction[13]);
  Multiplexer #(.select(3), .width(4), .enable("false")) multiplexer_3 (
    .in0(instruction[12:9]), .in1(instruction[12:9]), .in2(instruction[12:9]), .in3(4'b0100),
    .in4(multiplexer_1_out), .in5(multiplexer_2_out), .in6(4'b0100), .in7(4'b0100), .out(ALU_code),
    .sel(instruction[15:13]));
  or or_1 (jump, and_2_out, and_3_out);
  Comparator #(.width(4)) comparator_1 (.a(ALU_code), .b(4'b0100), .eq(comparator_1_eq));  // open: gt, lt
  Comparator #(.width(4)) comparator_2 (.a(ALU_code), .b(4'b0101), .eq(comparator_2_eq));  // open: gt, lt
  and and_5 (branch, and_4_out, ALU_output[0]);
  Multiplexer #(.select(3), .width(3), .enable("false")) multiplexer_4 (
    .in0(instruction[8:6]), .in1(instruction[8:6]), .in2(instruction[8:6]), .in3(instruction[11:9]),
    .in4(instruction[10:8]), .in5(instruction[11:9]), .in6(instruction[10:8]), .in7(3'b111), .out(rd),
    .sel(instruction[15:13]));
  and and_6 (inc_dec, check, or_2_out);
  or or_2 (or_2_out, comparator_1_eq, comparator_2_eq);
  assign bit_extender_1_out = {{4{1'b0}}, instruction[11:0]};  // Bit_Extender bit_extender_1
  Multiplexer #(.select(3), .width(3), .enable("false")) multiplexer_5 (
    .in0(3'b000), .in1(instruction[5:3]), .in2(instruction[5:3]), .in3(instruction[8:6]),
    .in4(instruction[10:8]), .in5(instruction[8:6]), .in6(instruction[10:8]), .in7(3'b000), .out(rs),
    .sel(instruction[15:13]));
  not not_5 (not_5_out, instruction[15]);
  and and_7 (MemOp, not_5_out, instruction[14], instruction[13]);
  Multiplexer #(.select(3), .width(16), .enable("false")) multiplexer_6 (
    .in5(signed_imm), .in6(ALU_output), .in7(bit_extender_1_out), .out(Branch_Value), .sel(instruction[15:13]));  // open: in0, in1, in2, in3, in4
  Multiplexer #(.select(3), .width(3), .enable("false")) multiplexer_7 (
    .in0(3'b000), .in1(3'b000), .in2(instruction[2:0]), .in3(instruction[11:9]), .in4(3'b000),
    .in5(instruction[11:9]), .in6(3'b000), .in7(3'b000), .out(rt), .sel(instruction[15:13]));
  assign signed_imm = {{10{instruction[5]}}, instruction[5:0]};  // Bit_Extender bit_extender_2
  Multiplexer #(.select(3), .enable("false")) multiplexer_8 (
    .in0(1'b0), .in1(1'b0), .in2(1'b0), .in3(instruction[12]), .in4(1'b0), .in5(1'b0), .in6(1'b0),
    .in7(1'b0), .out(lw_sw), .sel(instruction[15:13]));
  immediate_regwrite immediate_regwrite_1 (.opcode(instruction[15:11]), .ImmOp(ImmOp), .RegWrite(reg_write), .lui(lui));
  Adder #(.width(16)) adder_1 (.a(16'h1), .b(PC), .out(adder_1_out));  // open: cin, cout
  assign unsigned_imm = {{8{1'b0}}, instruction[7:0]};  // Bit_Extender bit_extender_3
  assign jrImm = {{8{instruction[7]}}, instruction[7:0]};  // Bit_Extender bit_extender_4
  Multiplexer #(.select(3), .width(16), .enable("false")) multiplexer_9 (
    .in0({16{1'b0}}), .in1({16{1'b0}}), .in2({16{1'b0}}), .in3(signed_imm), .in4(unsigned_imm),
    .in5(signed_imm), .in6(jrImm), .in7(adder_1_out), .out(immediate), .sel(instruction[15:13]));

  // Other names for the same wires on the sheet: ALU0[3:0] = instruction[12:9]; ALU1[3:0] = instruction[12:9];
  //   ALU2[3:0] = instruction[12:9]; op_code[1:0] = instruction[12:11]; rd3[2:0] = instruction[11:9];
  //   beq_blt = instruction[12]; lw_sw_t = instruction[12]; rt2[2:0] = instruction[2:0]; rs1[2:0] = instruction[5:3];
  //   rs2[2:0] = instruction[5:3]; rd0[2:0] = instruction[8:6]; rd1[2:0] = instruction[8:6];
  //   rd2[2:0] = instruction[8:6]; rs3[2:0] = instruction[8:6]; ALU[3:0] = ALU_code; rd4[2:0] = instruction[10:8]

  // Notes on the sheet:
  //   ZERO
  //   FIX REGWRITE
  //   UNARY
  //   jum
  //   BINARY
  //   LW/SW
  //   IMMEDIATE OP
  //   jal
endmodule

module immediate_regwrite (
  input  [4:0] opcode,
  output ImmOp,
  output RegWrite,
  output lui
);

  wire comparator_1_eq, comparator_2_eq, comparator_3_eq, comparator_4_eq, comparator_5_eq, comparator_6_eq,
       comparator_7_eq, comparator_8_eq, comparator_9_eq, comparator_10_eq, comparator_11_eq,
       comparator_12_eq, comparator_13_eq, comparator_14_eq, or_1_out, or_2_out;

  Comparator #(.width(3), .mode("unsigned")) comparator_1 (
    .a(opcode[4:2]), .b(3'b110), .eq(comparator_1_eq));  // open: gt, lt
  Comparator #(.width(4), .mode("unsigned")) comparator_2 (
    .a(opcode[4:1]), .b(4'b0110), .eq(comparator_2_eq));  // open: gt, lt
  Comparator #(.width(4), .mode("unsigned")) comparator_3 (
    .a(opcode[4:1]), .b(4'b1110), .eq(comparator_3_eq));  // open: gt, lt
  Comparator #(.width(4), .mode("unsigned")) comparator_4 (
    .a(opcode[4:1]), .b(4'b1111), .eq(comparator_4_eq));  // open: gt, lt
  Comparator #(.width(5), .mode("unsigned")) comparator_5 (
    .a(opcode), .b(5'b10000), .eq(comparator_5_eq));  // open: gt, lt
  Comparator #(.width(5), .mode("unsigned")) comparator_6 (
    .a(opcode), .b(5'b10001), .eq(comparator_6_eq));  // open: gt, lt
  Comparator #(.width(5), .mode("unsigned")) comparator_7 (
    .a(opcode), .b(5'b10010), .eq(comparator_7_eq));  // open: gt, lt
  Comparator #(.width(5), .mode("unsigned")) comparator_8 (
    .a(opcode), .b(5'b10011), .eq(comparator_8_eq));  // open: gt, lt
  Comparator #(.width(3), .mode("unsigned")) comparator_9 (
    .a(opcode[4:2]), .b(3'b000), .eq(comparator_9_eq));  // open: gt, lt
  Comparator #(.width(3), .mode("unsigned")) comparator_10 (
    .a(opcode[4:2]), .b(3'b001), .eq(comparator_10_eq));  // open: gt, lt
  Comparator #(.width(3), .mode("unsigned")) comparator_11 (
    .a(opcode[4:2]), .b(3'b010), .eq(comparator_11_eq));  // open: gt, lt
  Comparator #(.width(3), .mode("unsigned")) comparator_12 (
    .a(opcode[4:2]), .b(3'b100), .eq(comparator_12_eq));  // open: gt, lt
  Comparator #(.width(4), .mode("unsigned")) comparator_13 (
    .a(opcode[4:1]), .b(4'b1111), .eq(comparator_13_eq));  // open: gt, lt
  Comparator #(.width(4), .mode("unsigned")) comparator_14 (
    .a(opcode[4:1]), .b(4'b0110), .eq(comparator_14_eq));  // open: gt, lt
  Comparator #(.width(5)) comparator_15 (.a(opcode), .b(5'b10001), .eq(lui));  // open: gt, lt
  or or_1 (or_1_out, comparator_2_eq, comparator_3_eq, comparator_4_eq);
  or or_2 (or_2_out, comparator_5_eq, comparator_6_eq, comparator_7_eq, comparator_8_eq);
  or or_3 (ImmOp, comparator_1_eq, or_1_out, or_2_out);
  or or_4 (RegWrite, comparator_9_eq, comparator_10_eq, comparator_11_eq, comparator_12_eq, comparator_13_eq, comparator_14_eq);

  // Notes on the sheet:
  //   REGISTER WRITE
  //   IMMEDIATE OPERATION
  //   jr
  //   lw
  //   j
  //   jal
  //   ori
  //   lui
  //   addi
  //   subi
  //   0
  //   U
  //   B
  //   I
  //   jal
  //   lw
endmodule

module Hazard_Detection_Unit (
  input  [15:0] instruction,
  input  overflow,
  output exception
);

  wire and_1_out, and_2_out, and_3_out, comparator_1_eq, comparator_2_eq, comparator_3_eq, comparator_4_eq,
       comparator_5_eq, comparator_6_eq, not_1_out, not_2_out, not_3_out;

  Comparator #(.width(3), .mode("unsigned")) comparator_1 (
    .a(3'b000), .b(instruction[15:13]), .eq(comparator_1_eq));  // open: gt, lt
  Comparator #(.width(10), .mode("unsigned")) comparator_2 (
    .a({10{1'b0}}), .b({instruction[12:9], instruction[5:0]}), .eq(comparator_2_eq));  // open: gt, lt
  Comparator #(.width(3), .mode("unsigned")) comparator_3 (
    .a(3'b001), .b(instruction[15:13]), .eq(comparator_3_eq));  // open: gt, lt
  Comparator #(.width(3), .mode("unsigned")) comparator_4 (
    .a(3'b000), .b(instruction[2:0]), .eq(comparator_4_eq));  // open: gt, lt
  Comparator #(.width(3), .mode("unsigned")) comparator_5 (
    .a(3'b111), .b(instruction[15:13]), .eq(comparator_5_eq));  // open: gt, lt
  Comparator #(.width(2), .mode("unsigned")) comparator_6 (
    .a(2'b00), .b(instruction[12:11]), .eq(comparator_6_eq));  // open: gt, lt
  not not_1 (not_1_out, comparator_2_eq);
  not not_2 (not_2_out, comparator_4_eq);
  not not_3 (not_3_out, comparator_6_eq);
  and and_1 (and_1_out, comparator_1_eq, not_1_out);
  and and_2 (and_2_out, comparator_3_eq, not_2_out);
  and and_3 (and_3_out, comparator_5_eq, not_3_out);
  or or_1 (exception, overflow, and_1_out, and_2_out, and_3_out);

  // Notes on the sheet:
  //   ZERO
  //   UNARY
  //   JR
endmodule
