// Logisim project FD_Group01.circ as structural Verilog: 8 circuits, main circuit main
module main (
  output [15:0] pc,
  output [15:0] r0,
  output [15:0] r1,
  output [15:0] r2,
  output [15:0] r3,
  output [15:0] r4,
  output [15:0] r5,
  output [15:0] r6,
  output [15:0] r7,
  output halt
);

  wire and_1_out, clock_1_out, control_unit_1_branch, control_unit_1_immop, control_unit_1_jump,
       control_unit_1_memop, control_unit_1_regwrite, control_unit_1_sw, hazard_detection_unit_1_exception,
       n16_bit_alu_1_overflow, reset_out;
  wire [2:0] control_unit_1_rd, control_unit_1_rs, control_unit_1_rt;
  wire [3:0] control_unit_1_alu;
  wire [15:0] control_unit_1_branch_value, control_unit_1_immediate, multiplexer_1_out, multiplexer_2_out,
       n16_bit_alu_1_result, ram_1_data, ram_2_data, register_file_1_out_8, register_file_1_out_9;

  Halt halt_1 (
    .instruction(ram_1_data), .exception(hazard_detection_unit_1_exception), .halt(halt),
    .clock(clock_1_out), .reset(reset_out));
  Clock clock_1 (.out(clock_1_out));
  Button reset (.out(reset_out));
  and and_1 (and_1_out, ~halt, clock_1_out);  // AND_Gate
  PC pc_1 (
    .Branch__Value(control_unit_1_branch_value), .Reset(reset_out), .Instruction_Address(pc),
    .Branch_Relative(control_unit_1_branch), .Branch_Absolute(control_unit_1_jump), .Clock(and_1_out));
  Hazard_Detection_Unit hazard_detection_unit_1 (
    .instruction(ram_1_data), .exception(hazard_detection_unit_1_exception), .overflow(n16_bit_alu_1_overflow));
  RAM #(.addrWidth(16), .dataWidth(16), .bus("asynch")) ram_1 (.addr(pc), .data(ram_1_data));  // open: sel, ld, clr
  Control_Unit control_unit_1 (
    .instruction(ram_1_data), .rt(control_unit_1_rt), .rs(control_unit_1_rs),
    .alu_output(n16_bit_alu_1_result), .branch_value(control_unit_1_branch_value), .PC(pc),
    .immediate(control_unit_1_immediate), .alu(control_unit_1_alu), .rd(control_unit_1_rd),
    .sw(control_unit_1_sw), .MemOp(control_unit_1_memop), .jump(control_unit_1_jump),
    .branch(control_unit_1_branch), .ImmOp(control_unit_1_immop), .regWrite(control_unit_1_regwrite));
  Register_File register_file_1 (
    .Data(multiplexer_2_out), .write(control_unit_1_regwrite), .rd(control_unit_1_rd), .reset(reset_out),
    .clock(and_1_out), .rs(control_unit_1_rs), .out_8(register_file_1_out_8), .rt(control_unit_1_rt),
    .out_9(register_file_1_out_9), .r0(r0), .r1(r1), .r2(r2), .r3(r3), .r4(r4), .r5(r5), .r6(r6), .r7(r7));
  Multiplexer #(.width(16), .enable("false")) multiplexer_1 (
    .in0(register_file_1_out_9), .in1(control_unit_1_immediate), .out(multiplexer_1_out),
    .sel(control_unit_1_immop));
  _16_bit_ALU u_16_bit_alu_1 (
    .ALU_code(control_unit_1_alu), .a(register_file_1_out_8), .b(multiplexer_1_out),
    .overflow(n16_bit_alu_1_overflow), .result(n16_bit_alu_1_result));
  Multiplexer #(.width(16), .enable("false")) multiplexer_2 (
    .in0(n16_bit_alu_1_result), .in1(ram_2_data), .out(multiplexer_2_out), .sel(control_unit_1_memop));
  RAM #(.addrWidth(16), .dataWidth(16), .bus("separate")) ram_2 (
    .addr(n16_bit_alu_1_result), .din(register_file_1_out_9), .data(ram_2_data), .str(control_unit_1_sw),
    .clk(and_1_out), .ld(1'b1));  // open: sel, clr

  // Notes on the sheet:
  //   current instruction
  //   clock signal
  //   reset button
  //   DO NOT CHANGE THE INPUTS AND OUTPUTS OF THIS CIRCUIT! Do not add/remove inputs or outputs. Do not even change their location or orientation.
endmodule

module Halt (
  input  [15:0] instruction,
  input  exception,
  input  clock,
  input  reset,
  output halt
);

  wire and_1_out, comparator_1_eq, comparator_2_gt, counter_1_carry, or_1_out, or_2_out, register_1_q;
  wire [11:0] counter_1_q;

  Comparator #(.width(16), .mode("unsigned")) comparator_1 (
    .a(instruction), .b({16{1'b0}}), .eq(comparator_1_eq));  // open: gt, lt
  Counter #(.width(12), .max('hfff), .trigger("falling")) counter_1 (
    .Q(counter_1_q), .carry(counter_1_carry), .clk(clock), .clr(reset));  // open: load, D, count
  or or_1 (or_1_out, comparator_1_eq, counter_1_carry);
  Comparator #(.width(12), .mode("unsigned")) comparator_2 (
    .a(counter_1_q), .b({12{1'b0}}), .gt(comparator_2_gt));  // open: eq, lt
  or or_2 (or_2_out, register_1_q, and_1_out);
  and and_1 (and_1_out, or_1_out, comparator_2_gt);
  Register_part #(.width(1)) register_1 (.D(or_2_out), .Q(register_1_q), .clk(clock), .clr(reset));  // open: en
  or or_3 (halt, exception, register_1_q);

  // Notes on the sheet:
  //   halt becomes and stays asserted if the instruction is 0000 (not in the first clock cycle) or the end of the counter is reached (2^12)
endmodule

module Register (
  input  reset,
  input  write,
  input  clock,
  input  [15:0] D,
  output [15:0] Q
);

  D_Flip_Flop #(.trigger("falling")) d_ff_1 (
    .clk(clock), .D(D[0]), .Q(Q[0]), .en(write), .reset(reset));  // open: Qn, preset
  D_Flip_Flop #(.trigger("falling")) d_ff_2 (
    .clk(clock), .D(D[1]), .Q(Q[1]), .en(write), .reset(reset));  // open: Qn, preset
  D_Flip_Flop #(.trigger("falling")) d_ff_3 (
    .clk(clock), .D(D[2]), .Q(Q[2]), .en(write), .reset(reset));  // open: Qn, preset
  D_Flip_Flop #(.trigger("falling")) d_ff_4 (
    .clk(clock), .D(D[3]), .Q(Q[3]), .en(write), .reset(reset));  // open: Qn, preset
  D_Flip_Flop #(.trigger("falling")) d_ff_5 (
    .clk(clock), .D(D[4]), .Q(Q[4]), .en(write), .reset(reset));  // open: Qn, preset
  D_Flip_Flop #(.trigger("falling")) d_ff_6 (
    .clk(clock), .D(D[5]), .Q(Q[5]), .en(write), .reset(reset));  // open: Qn, preset
  D_Flip_Flop #(.trigger("falling")) d_ff_7 (
    .clk(clock), .D(D[6]), .Q(Q[6]), .en(write), .reset(reset));  // open: Qn, preset
  D_Flip_Flop #(.trigger("falling")) d_ff_8 (
    .clk(clock), .D(D[7]), .Q(Q[7]), .en(write), .reset(reset));  // open: Qn, preset
  D_Flip_Flop #(.trigger("falling")) d_ff_9 (
    .clk(clock), .D(D[8]), .Q(Q[8]), .en(write), .reset(reset));  // open: Qn, preset
  D_Flip_Flop #(.trigger("falling")) d_ff_10 (
    .clk(clock), .D(D[9]), .Q(Q[9]), .en(write), .reset(reset));  // open: Qn, preset
  D_Flip_Flop #(.trigger("falling")) d_ff_11 (
    .clk(clock), .D(D[10]), .Q(Q[10]), .en(write), .reset(reset));  // open: Qn, preset
  D_Flip_Flop #(.trigger("falling")) d_ff_12 (
    .clk(clock), .D(D[11]), .Q(Q[11]), .en(write), .reset(reset));  // open: Qn, preset
  D_Flip_Flop #(.trigger("falling")) d_ff_13 (
    .clk(clock), .D(D[12]), .Q(Q[12]), .en(write), .reset(reset));  // open: Qn, preset
  D_Flip_Flop #(.trigger("falling")) d_ff_14 (
    .clk(clock), .D(D[13]), .Q(Q[13]), .en(write), .reset(reset));  // open: Qn, preset
  D_Flip_Flop #(.trigger("falling")) d_ff_15 (
    .clk(clock), .D(D[14]), .Q(Q[14]), .en(write), .reset(reset));  // open: Qn, preset
  D_Flip_Flop #(.trigger("falling")) d_ff_16 (
    .clk(clock), .D(D[15]), .Q(Q[15]), .en(write), .reset(reset));  // open: Qn, preset
endmodule

module PC (
  input  Branch_Relative,
  input  Branch_Absolute,
  input  Clock,
  input  [15:0] Branch__Value,
  input  Reset,
  output [15:0] Instruction_Address
);

  wire and_1_out, nand_1_out, not_1_out, not_2_out, or_1_out;
  wire [15:0] adder_1_out, multiplexer_1_out, multiplexer_2_out;

  Multiplexer #(.width(16), .enable("false")) multiplexer_1 (
    .in0({16{1'b0}}), .in1(Branch__Value), .out(multiplexer_1_out), .sel(Branch_Relative));
  not not_1 (not_1_out, Branch_Relative);
  not not_2 (not_2_out, Branch_Absolute);
  and and_1 (and_1_out, not_1_out, not_2_out);
  or or_1 (or_1_out, Branch_Relative, and_1_out);
  Adder #(.width(16)) adder_1 (
    .a(multiplexer_1_out), .b(Instruction_Address), .out(adder_1_out), .cin(or_1_out));  // open: cout
  Multiplexer #(.width(16), .enable("false")) multiplexer_2 (
    .in0(adder_1_out), .in1(Branch__Value), .out(multiplexer_2_out), .sel(Branch_Absolute));
  nand nand_1 (nand_1_out, Branch_Relative, Branch_Absolute);
  Register register_1 (
    .D(multiplexer_2_out), .reset(Reset), .write(nand_1_out), .clock(Clock), .Q(Instruction_Address));
endmodule

module Register_File (
  input  write,
  input  [2:0] rd,
  input  reset,
  input  clock,
  input  [2:0] rs,
  input  [2:0] rt,
  input  [15:0] Data,
  output [15:0] out_8,
  output [15:0] out_9,
  output [15:0] r0,
  output [15:0] r1,
  output [15:0] r2,
  output [15:0] r3,
  output [15:0] r4,
  output [15:0] r5,
  output [15:0] r6,
  output [15:0] r7
);

  wire demultiplexer_1_out1, demultiplexer_1_out2, demultiplexer_1_out3, demultiplexer_1_out4,
       demultiplexer_1_out5, demultiplexer_1_out6, demultiplexer_1_out7;

  Demultiplexer #(.select(3), .enable("false")) demultiplexer_1 (
    .out1(demultiplexer_1_out1), .out2(demultiplexer_1_out2), .out3(demultiplexer_1_out3),
    .out4(demultiplexer_1_out4), .out5(demultiplexer_1_out5), .out6(demultiplexer_1_out6),
    .out7(demultiplexer_1_out7), .in(write), .sel(rd));  // open: out0
  Register register_1 (.D(Data), .reset(reset), .write(demultiplexer_1_out1), .clock(clock), .Q(r1));
  Register register_2 (.D(Data), .reset(reset), .write(demultiplexer_1_out2), .clock(clock), .Q(r2));
  Register register_3 (.D(Data), .reset(reset), .write(demultiplexer_1_out3), .clock(clock), .Q(r3));
  Register register_4 (.D(Data), .reset(reset), .write(demultiplexer_1_out4), .clock(clock), .Q(r4));
  Register register_5 (.D(Data), .reset(reset), .write(demultiplexer_1_out5), .clock(clock), .Q(r5));
  Register register_6 (.D(Data), .reset(reset), .write(demultiplexer_1_out6), .clock(clock), .Q(r6));
  Register register_7 (.D(Data), .reset(reset), .write(demultiplexer_1_out7), .clock(clock), .Q(r7));
  Multiplexer #(.select(3), .width(16), .enable("false")) multiplexer_1 (
    .in0({16{1'b0}}), .in1(r1), .in2(r2), .in3(r3), .in4(r4), .in5(r5), .in6(r6), .in7(r7), .out(out_8),
    .sel(rs));
  Multiplexer #(.select(3), .width(16), .enable("false")) multiplexer_2 (
    .in0({16{1'b0}}), .in1(r1), .in2(r2), .in3(r3), .in4(r4), .in5(r5), .in6(r6), .in7(r7), .out(out_9),
    .sel(rt));

  assign r0 = {16{1'b0}};
endmodule

module Control_Unit (
  input  [15:0] instruction,
  input  [15:0] alu_output,
  input  [15:0] PC,
  output sw,
  output MemOp,
  output branch,
  output jump,
  output [15:0] immediate,
  output [15:0] branch_value,
  output [3:0] alu,
  output [2:0] rd,
  output [2:0] rs,
  output [2:0] rt,
  output ImmOp,
  output regWrite
);

  wire and_2_out, comparator_1_eq, comparator_2_eq, comparator_3_eq, comparator_4_eq, comparator_6_eq,
       comparator_7_eq, comparator_8_eq, comparator_9_eq, comparator_10_eq, comparator_11_eq,
       comparator_12_eq, comparator_13_eq, comparator_14_eq, comparator_15_eq, comparator_16_eq,
       comparator_17_eq, multiplexer_1_out, or_1_out, or_2_out, or_3_out, or_4_out, or_5_out, or_7_out,
       or_9_out;
  wire [2:0] controlled_buffer_10_out;
  wire [15:0] adder_1_out, bit_extender_1_out, bit_extender_2_out, bit_extender_3_out, bit_extender_4_out;

  assign bit_extender_1_out = {{10{instruction[5]}}, instruction[5:0]};  // Bit_Extender bit_extender_1
  assign bit_extender_2_out = {{8{instruction[7]}}, instruction[7:0]};  // Bit_Extender bit_extender_2
  assign bit_extender_3_out = {{8{1'b0}}, instruction[7:0]};  // Bit_Extender bit_extender_3
  assign bit_extender_4_out = {{4{1'b0}}, instruction[11:0]};  // Bit_Extender bit_extender_4
  Comparator #(.width(3), .mode("unsigned")) comparator_1 (
    .a(instruction[15:13]), .b(3'b000), .eq(comparator_1_eq));  // open: gt, lt
  Comparator #(.width(3), .mode("unsigned")) comparator_2 (
    .a(instruction[15:13]), .b(3'b001), .eq(comparator_2_eq));  // open: gt, lt
  Comparator #(.width(3), .mode("unsigned")) comparator_3 (
    .a(instruction[15:13]), .b(3'b010), .eq(comparator_3_eq));  // open: gt, lt
  Comparator #(.width(4), .mode("unsigned")) comparator_4 (
    .a(instruction[15:12]), .b(4'b0110), .eq(comparator_4_eq));  // open: gt, lt
  Comparator #(.width(4), .mode("unsigned")) comparator_5 (
    .a(instruction[15:12]), .b(4'b0111), .eq(sw));  // open: gt, lt
  Comparator #(.width(4), .mode("unsigned")) comparator_6 (
    .a(instruction[15:12]), .b(4'b1010), .eq(comparator_6_eq));  // open: gt, lt
  Comparator #(.width(4), .mode("unsigned")) comparator_7 (
    .a(instruction[15:12]), .b(4'b1011), .eq(comparator_7_eq));  // open: gt, lt
  Comparator #(.width(5), .mode("unsigned")) comparator_8 (
    .a(instruction[15:11]), .b(5'b10000), .eq(comparator_8_eq));  // open: gt, lt
  Comparator #(.width(5), .mode("unsigned")) comparator_9 (
    .a(instruction[15:11]), .b(5'b10001), .eq(comparator_9_eq));  // open: gt, lt
  Comparator #(.width(5), .mode("unsigned")) comparator_10 (
    .a(instruction[15:11]), .b(5'b10010), .eq(comparator_10_eq));  // open: gt, lt
  Comparator #(.width(5), .mode("unsigned")) comparator_11 (
    .a(instruction[15:11]), .b(5'b10011), .eq(comparator_11_eq));  // open: gt, lt
  Comparator #(.width(5), .mode("unsigned")) comparator_12 (
    .a(instruction[15:11]), .b(5'b11000), .eq(comparator_12_eq));  // open: gt, lt
  Comparator #(.width(4), .mode("unsigned")) comparator_13 (
    .a(instruction[15:12]), .b(4'b1110), .eq(comparator_13_eq));  // open: gt, lt
  or or_1 (or_1_out, comparator_13_eq, comparator_14_eq);
  Comparator #(.width(4), .mode("unsigned")) comparator_14 (
    .a(instruction[15:12]), .b(4'b1111), .eq(comparator_14_eq));  // open: gt, lt
  or or_2 (or_2_out, comparator_1_eq, comparator_2_eq, comparator_3_eq);
  or or_3 (or_3_out, comparator_7_eq, comparator_6_eq);
  Comparator #(.width(16), .mode("unsigned")) comparator_15 (
    .a(16'h1), .b(alu_output), .eq(comparator_15_eq));  // open: gt, lt
  assign immediate = comparator_9_eq ? {bit_extender_3_out[7:0], {8{1'b0}}} : 16'bz;  // Controlled_Buffer controlled_buffer_1
  assign branch_value = or_1_out ? bit_extender_4_out : 16'bz;  // Controlled_Buffer controlled_buffer_2
  assign alu = or_2_out ? instruction[12:9] : 4'bz;  // Controlled_Buffer controlled_buffer_3
  assign rd = or_2_out ? instruction[8:6] : 3'bz;  // Controlled_Buffer controlled_buffer_4
  assign rs = or_2_out ? instruction[5:3] : 3'bz;  // Controlled_Buffer controlled_buffer_5
  assign rt = or_2_out ? instruction[2:0] : 3'bz;  // Controlled_Buffer controlled_buffer_6
  or or_4 (or_4_out, comparator_4_eq, sw, comparator_6_eq, comparator_7_eq);
  assign rd = or_4_out ? instruction[11:9] : 3'bz;  // Controlled_Buffer controlled_buffer_7
  assign rs = or_4_out ? instruction[8:6] : 3'bz;  // Controlled_Buffer controlled_buffer_8
  assign immediate = or_4_out ? bit_extender_1_out : 16'bz;  // Controlled_Buffer controlled_buffer_9
  and and_1 (branch, or_3_out, comparator_15_eq);
  or or_5 (or_5_out, comparator_11_eq, comparator_10_eq, comparator_9_eq, comparator_8_eq);
  assign controlled_buffer_10_out = comparator_12_eq ? instruction[10:8] : 3'bz;  // Controlled_Buffer controlled_buffer_10
  Multiplexer #(.enable("false")) multiplexer_1 (
    .in0(or_5_out), .in1(1'b0), .out(multiplexer_1_out), .sel(comparator_9_eq));
  assign immediate = comparator_12_eq ? bit_extender_2_out : 16'bz;  // Controlled_Buffer controlled_buffer_11
  assign branch_value = comparator_12_eq ? alu_output : 16'bz;  // Controlled_Buffer controlled_buffer_12
  immediate_regwrite immediate_regwrite_1 (.opcode(instruction[15:9]), .ImmOp(ImmOp), .RegWrite(regWrite));
  assign rd = or_5_out ? instruction[10:8] : 3'bz;  // Controlled_Buffer controlled_buffer_13
  assign controlled_buffer_10_out = or_5_out ? instruction[10:8] : 3'bz;  // Controlled_Buffer controlled_buffer_14
  assign immediate = multiplexer_1_out ? bit_extender_3_out : 16'bz;  // Controlled_Buffer controlled_buffer_15
  or or_6 (jump, comparator_12_eq, or_1_out);
  Adder #(.width(16)) adder_1 (.a(16'h1), .b(PC), .out(adder_1_out));  // open: cin, cout
  or or_7 (or_7_out, comparator_12_eq, comparator_10_eq);
  assign alu = or_7_out ? 4'b0100 : 4'bz;  // Controlled_Buffer controlled_buffer_16
  assign alu = comparator_11_eq ? 4'b0101 : 4'bz;  // Controlled_Buffer controlled_buffer_17
  assign rs = or_1_out ? 3'b000 : 3'bz;  // Controlled_Buffer controlled_buffer_18
  assign alu = or_1_out ? 4'b0100 : 4'bz;  // Controlled_Buffer controlled_buffer_19
  assign rd = or_1_out ? 3'b111 : 3'bz;  // Controlled_Buffer controlled_buffer_20
  assign immediate = or_1_out ? adder_1_out : 16'bz;  // Controlled_Buffer controlled_buffer_21
  Comparator #(.width(4), .mode("unsigned")) comparator_16 (
    .a(alu), .b(4'b0100), .eq(comparator_16_eq));  // open: gt, lt
  Comparator #(.width(4), .mode("unsigned")) comparator_17 (
    .a(alu), .b(4'b0101), .eq(comparator_17_eq));  // open: gt, lt
  or or_8 (MemOp, sw, comparator_4_eq);
  assign alu = comparator_9_eq ? 4'b0100 : 4'bz;  // Controlled_Buffer controlled_buffer_22
  Multiplexer #(.width(3), .enable("false")) multiplexer_2 (
    .in0(controlled_buffer_10_out), .in1(3'b000), .out(rs), .sel(comparator_9_eq));
  assign rd = comparator_12_eq ? 3'b000 : 3'bz;  // Controlled_Buffer controlled_buffer_23
  or or_9 (or_9_out, comparator_16_eq, comparator_17_eq);
  assign alu = MemOp ? 4'b0100 : 4'bz;  // Controlled_Buffer controlled_buffer_24
  assign alu = comparator_6_eq ? 4'b1000 : 4'bz;  // Controlled_Buffer controlled_buffer_25
  assign alu = comparator_7_eq ? 4'b1001 : 4'bz;  // Controlled_Buffer controlled_buffer_26
  assign alu = comparator_8_eq ? 4'b0011 : 4'bz;  // Controlled_Buffer controlled_buffer_27
  and and_2 (and_2_out, or_2_out, or_9_out);
  assign immediate = and_2_out ? 16'h1 : 16'bz;  // Controlled_Buffer controlled_buffer_28
  assign rt = or_4_out ? rd : 3'bz;  // Controlled_Buffer controlled_buffer_29
  assign branch_value = or_3_out ? immediate : 16'bz;  // Controlled_Buffer controlled_buffer_30

  // Notes on the sheet:
  //   OP
  //   ALU
  //   rd
  //   rs
  //   rt
  //   OP
  //   rd
  //   rs
  //   imm
  //   OP
  //   rd
  //   imm
  //   OP
  //   adr
  //   ZERO & UNARY & BINARY
  //   LW/SW & BEQ/BLT
  //   IMMEDIATE & JR
  //   J & JAL
  //   lw
  //   sw
  //   beq
  //   blt
  //   ori
  //   lui
  //   addi
  //   subi
  //   jr
  //   j
  //   jal
  //   inc
  //   dec
endmodule

module immediate_regwrite (
  input  [6:0] opcode,
  output ImmOp,
  output RegWrite
);

  wire comparator_1_eq, comparator_2_eq, comparator_3_eq, comparator_4_eq, comparator_5_eq, comparator_6_eq,
       comparator_7_eq, comparator_8_eq, comparator_9_eq, comparator_10_eq, comparator_11_eq,
       comparator_12_eq, comparator_13_eq, comparator_14_eq, comparator_15_eq, comparator_16_eq,
       comparator_17_eq;

  Comparator #(.width(7), .mode("unsigned")) comparator_1 (
    .a(opcode), .b(7'b0010100), .eq(comparator_1_eq));  // open: gt, lt
  Comparator #(.width(7), .mode("unsigned")) comparator_2 (
    .a(opcode), .b(7'b0010101), .eq(comparator_2_eq));  // open: gt, lt
  Comparator #(.width(3), .mode("unsigned")) comparator_3 (
    .a(opcode[6:4]), .b(3'b110), .eq(comparator_3_eq));  // open: gt, lt
  Comparator #(.width(4), .mode("unsigned")) comparator_4 (
    .a(opcode[6:3]), .b(4'b0110), .eq(comparator_4_eq));  // open: gt, lt
  Comparator #(.width(4), .mode("unsigned")) comparator_5 (
    .a(opcode[6:3]), .b(4'b0111), .eq(comparator_5_eq));  // open: gt, lt
  Comparator #(.width(4), .mode("unsigned")) comparator_6 (
    .a(opcode[6:3]), .b(4'b1110), .eq(comparator_6_eq));  // open: gt, lt
  Comparator #(.width(4), .mode("unsigned")) comparator_7 (
    .a(opcode[6:3]), .b(4'b1111), .eq(comparator_7_eq));  // open: gt, lt
  Comparator #(.width(5), .mode("unsigned")) comparator_8 (
    .a(opcode[6:2]), .b(5'b10000), .eq(comparator_8_eq));  // open: gt, lt
  Comparator #(.width(5), .mode("unsigned")) comparator_9 (
    .a(opcode[6:2]), .b(5'b10001), .eq(comparator_9_eq));  // open: gt, lt
  Comparator #(.width(5), .mode("unsigned")) comparator_10 (
    .a(opcode[6:2]), .b(5'b10010), .eq(comparator_10_eq));  // open: gt, lt
  Comparator #(.width(5), .mode("unsigned")) comparator_11 (
    .a(opcode[6:2]), .b(5'b10011), .eq(comparator_11_eq));  // open: gt, lt
  Comparator #(.width(3), .mode("unsigned")) comparator_12 (
    .a(opcode[6:4]), .b(3'b000), .eq(comparator_12_eq));  // open: gt, lt
  Comparator #(.width(3), .mode("unsigned")) comparator_13 (
    .a(opcode[6:4]), .b(3'b001), .eq(comparator_13_eq));  // open: gt, lt
  Comparator #(.width(3), .mode("unsigned")) comparator_14 (
    .a(opcode[6:4]), .b(3'b010), .eq(comparator_14_eq));  // open: gt, lt
  Comparator #(.width(3), .mode("unsigned")) comparator_15 (
    .a(opcode[6:4]), .b(3'b100), .eq(comparator_15_eq));  // open: gt, lt
  Comparator #(.width(4), .mode("unsigned")) comparator_16 (
    .a(opcode[6:3]), .b(4'b1111), .eq(comparator_16_eq));  // open: gt, lt
  Comparator #(.width(4), .mode("unsigned")) comparator_17 (
    .a(opcode[6:3]), .b(4'b0110), .eq(comparator_17_eq));  // open: gt, lt
  or or_1 (RegWrite, comparator_12_eq, comparator_13_eq, comparator_14_eq, comparator_15_eq, comparator_16_eq, comparator_17_eq);
  or or_2 (ImmOp, comparator_1_eq, comparator_2_eq, comparator_3_eq, comparator_4_eq, comparator_5_eq, comparator_6_eq, comparator_7_eq, comparator_8_eq, comparator_9_eq, comparator_10_eq, comparator_11_eq);

  // Notes on the sheet:
  //   inc
  //   dec
  //   jr
  //   lw
  //   sw
  //   j
  //   jal
  //   ori
  //   lui
  //   addi
  //   subi
  //   REGISTER WRITE
  //   0
  //   U
  //   B
  //   I
  //   jal
  //   lw
  //   IMMEDIATE OPERATION
endmodule

module Hazard_Detection_Unit (
  input  [15:0] instruction,
  input  overflow,
  output exception
);

  wire and_1_out, and_2_out, and_3_out, comparator_1_eq, comparator_2_eq, comparator_3_eq, comparator_4_eq,
       comparator_5_eq, comparator_6_eq, not_1_out, not_2_out, not_3_out;

  Comparator #(.width(3), .mode("unsigned")) comparator_1 (
    .a(3'b000), .b(instruction[15:13]), .eq(comparator_1_eq));  // open: gt, lt
  Comparator #(.width(10), .mode("unsigned")) comparator_2 (
    .a({10{1'b0}}), .b({instruction[12:9], instruction[5:0]}), .eq(comparator_2_eq));  // open: gt, lt
  Comparator #(.width(3), .mode("unsigned")) comparator_3 (
    .a(3'b001), .b(instruction[15:13]), .eq(comparator_3_eq));  // open: gt, lt
  Comparator #(.width(3), .mode("unsigned")) comparator_4 (
    .a(3'b000), .b(instruction[2:0]), .eq(comparator_4_eq));  // open: gt, lt
  Comparator #(.width(3), .mode("unsigned")) comparator_5 (
    .a(3'b110), .b(instruction[15:13]), .eq(comparator_5_eq));  // open: gt, lt
  Comparator #(.width(2), .mode("unsigned")) comparator_6 (
    .a(2'b00), .b(instruction[12:11]), .eq(comparator_6_eq));  // open: gt, lt
  not not_1 (not_1_out, comparator_2_eq);
  not not_2 (not_2_out, comparator_4_eq);
  not not_3 (not_3_out, comparator_6_eq);
  and and_1 (and_1_out, comparator_1_eq, not_1_out);
  and and_2 (and_2_out, comparator_3_eq, not_2_out);
  and and_3 (and_3_out, comparator_5_eq, not_3_out);
  or or_1 (exception, overflow, and_1_out, and_2_out, and_3_out);

  // Notes on the sheet:
  //   ZERO
  //   UNARY
  //   JR
endmodule
