// Logisim project project1.circ as structural Verilog: 5 circuits, main circuit 1a
module _1a (
  input  in_1,
  input  in_2,
  output out_3
);

  wire and_1_out;

  and and_1 (and_1_out, in_1, in_2);
  not not_1 (out_3, and_1_out);

  // Notes on the sheet:
  //   NAND from AND and NOT gates
endmodule

module _1b (
  input  in_1,
  input  in_2,
  input  in_3,
  input  in_4,
  input  in_5,
  input  in_6,
  input  in_7,
  input  in_8,
  input  in_9,
  input  in_10,
  input  in_11,
  input  in_12,
  input  in_13,
  input  in_14,
  input  in_15,
  input  in_16,
  input  in_17,
  input  in_18,
  output out_19,
  output out_20,
  output out_21,
  output out_22,
  output out_23,
  output out_24,
  output out_25,
  output out_26,
  output out_27,
  output out_28
);

  wire n1a_1_out_3, n1a_2_out_3, n1a_3_out_3, n1a_4_out_3, n1a_5_out_3, n1a_6_out_3, n1a_12_out_3,
       n1a_13_out_3, n1a_14_out_3, n1a_15_out_3, n1a_17_out_3, n1a_19_out_3;

  _1a u_1a_1 (.in_1(in_1), .in_2(in_3), .out_3(n1a_1_out_3));
  _1a u_1a_2 (.in_1(in_5), .in_2(in_7), .out_3(n1a_2_out_3));
  _1a u_1a_3 (.in_1(in_9), .in_2(in_9), .out_3(n1a_3_out_3));
  _1a u_1a_4 (.in_1(in_11), .in_2(in_11), .out_3(n1a_4_out_3));
  _1a u_1a_5 (.in_1(in_13), .in_2(in_13), .out_3(n1a_5_out_3));
  _1a u_1a_6 (.in_1(in_15), .in_2(in_15), .out_3(n1a_6_out_3));
  _1a u_1a_7 (.in_1(in_17), .in_2(in_17), .out_3(out_27));
  _1a u_1a_8 (.in_1(n1a_1_out_3), .in_2(n1a_1_out_3), .out_3(out_19));
  _1a u_1a_9 (.in_1(n1a_2_out_3), .in_2(n1a_2_out_3), .out_3(out_21));
  _1a u_1a_10 (.in_1(n1a_3_out_3), .in_2(n1a_4_out_3), .out_3(out_23));
  _1a u_1a_11 (.in_1(n1a_5_out_3), .in_2(n1a_6_out_3), .out_3(out_25));
  _1a u_1a_12 (.in_1(in_10), .in_2(in_10), .out_3(n1a_12_out_3));
  _1a u_1a_13 (.in_1(in_12), .in_2(in_12), .out_3(n1a_13_out_3));
  _1a u_1a_14 (.in_1(in_14), .in_2(in_14), .out_3(n1a_14_out_3));
  _1a u_1a_15 (.in_1(in_16), .in_2(in_16), .out_3(n1a_15_out_3));
  _1a u_1a_16 (.in_1(in_18), .in_2(in_18), .out_3(out_28));
  _1a u_1a_17 (.in_1(in_2), .in_2(in_4), .out_3(n1a_17_out_3));
  _1a u_1a_18 (.in_1(n1a_17_out_3), .in_2(n1a_17_out_3), .out_3(out_20));
  _1a u_1a_19 (.in_1(in_6), .in_2(in_8), .out_3(n1a_19_out_3));
  _1a u_1a_20 (.in_1(n1a_19_out_3), .in_2(n1a_19_out_3), .out_3(out_22));
  _1a u_1a_21 (.in_1(n1a_12_out_3), .in_2(n1a_13_out_3), .out_3(out_24));
  _1a u_1a_22 (.in_1(n1a_14_out_3), .in_2(n1a_15_out_3), .out_3(out_26));

  // Notes on the sheet:
  //   AND from NAND
  //   OR from NAND
  //   NOT from NAND
endmodule

module _2 (
  input  A,
  input  B,
  input  C,
  output X,
  output Y
);

  wire and_1_out, and_2_out, and_3_out, not_1_out, not_2_out, not_3_out;

  not not_1 (not_1_out, A);
  not not_2 (not_2_out, B);
  not not_3 (not_3_out, C);
  and and_1 (and_1_out, not_1_out, not_2_out);
  and and_2 (and_2_out, not_2_out, not_3_out);
  and and_3 (and_3_out, not_1_out, not_2_out);
  or or_1 (X, and_1_out, and_2_out);
  or or_2 (Y, and_3_out, not_3_out);

  // Notes on the sheet:
  //   X = ~A~B + ~B~C
  //   Y = ~A~B + ~C
  //   The boolean expressions associated with the given truth table:
  //   Truth table from question 2 converted to logic
endmodule

module _3 (
  input  x,
  input  y,
  input  z,
  output a,
  output b,
  output c,
  output d,
  output e,
  output f,
  output g,
  output h
);

  wire and_1_out, and_2_out, and_3_out, and_4_out, and_5_out, and_6_out, and_7_out, and_8_out, and_9_out,
       and_10_out, and_11_out, and_12_out, and_13_out, and_14_out, and_15_out, and_16_out, not_1_out,
       not_2_out, not_3_out, not_4_out, not_5_out, not_6_out, not_7_out, not_8_out, not_9_out, not_10_out,
       not_11_out, not_12_out, not_13_out, not_14_out, not_15_out, not_16_out, not_17_out, not_18_out,
       not_19_out, not_20_out, not_21_out;

  not not_1 (not_1_out, x);
  not not_2 (not_2_out, y);
  not not_3 (not_3_out, z);
  not not_4 (not_4_out, y);
  not not_5 (not_5_out, z);
  not not_6 (not_6_out, y);
  not not_7 (not_7_out, z);
  not not_8 (not_8_out, x);
  not not_9 (not_9_out, z);
  not not_10 (not_10_out, y);
  not not_11 (not_11_out, z);
  not not_12 (not_12_out, x);
  not not_13 (not_13_out, z);
  not not_14 (not_14_out, z);
  not not_15 (not_15_out, x);
  not not_16 (not_16_out, z);
  not not_17 (not_17_out, x);
  not not_18 (not_18_out, z);
  not not_19 (not_19_out, y);
  not not_20 (not_20_out, y);
  and and_1 (and_1_out, not_1_out, y);
  and and_2 (and_2_out, x, not_2_out);
  and and_3 (and_3_out, x, not_3_out);
  and and_4 (and_4_out, not_4_out, not_5_out);
  and and_5 (and_5_out, x, not_6_out);
  and and_6 (and_6_out, x, not_7_out);
  and and_7 (and_7_out, not_8_out, not_9_out);
  and and_8 (and_8_out, x, z);
  not not_21 (not_21_out, x);
  and and_9 (and_9_out, not_10_out, not_11_out);
  and and_10 (and_10_out, y, z);
  and and_11 (and_11_out, not_12_out, not_13_out);
  and and_12 (and_12_out, y, not_14_out);
  and and_13 (and_13_out, not_15_out, not_16_out);
  and and_14 (and_14_out, not_17_out, y);
  and and_15 (and_15_out, y, not_18_out);
  and and_16 (and_16_out, x, not_19_out, z);
  or or_1 (g, not_20_out, z, x);
  or or_2 (a, and_1_out, and_2_out, and_3_out);
  or or_3 (b, and_4_out, and_5_out, and_6_out);
  or or_4 (c, and_7_out, y, and_8_out);
  or or_5 (d, not_21_out, and_9_out, and_10_out);
  or or_6 (e, and_11_out, and_12_out);
  or or_7 (f, and_13_out, and_14_out, and_15_out, and_16_out);

  assign h = 1'b0;
endmodule

module _3_display (
  input  [2:0] in_1
);

  wire n3_1_a, n3_1_b, n3_1_c, n3_1_d, n3_1_e, n3_1_f, n3_1_g;

  _3 u_3_1 (
    .x(in_1[2]), .y(in_1[1]), .z(in_1[0]), .a(n3_1_a), .b(n3_1_b), .c(n3_1_c), .d(n3_1_d), .e(n3_1_e),
    .f(n3_1_f), .g(n3_1_g));  // open: h
  _7_Segment_Display u_7_segment_display_1 (
    .g(n3_1_a), .f(n3_1_b), .a(n3_1_c), .b(n3_1_d), .e(n3_1_e), .d(n3_1_f), .c(n3_1_g));  // open: dp
endmodule
