// Logisim project project4.circ as structural Verilog: 5 circuits, main circuit 16-bit register
module _16_bit_register (
  input  reset,
  input  write,
  input  clock,
  input  [15:0] D,
  output [15:0] Q
);

  D_Flip_Flop #(.trigger("falling")) d_ff_1 (
    .clk(clock), .D(D[0]), .Q(Q[0]), .en(write), .reset(reset));  // open: Qn, preset
  D_Flip_Flop #(.trigger("falling")) d_ff_2 (
    .clk(clock), .D(D[1]), .Q(Q[1]), .en(write), .reset(reset));  // open: Qn, preset
  D_Flip_Flop #(.trigger("falling")) d_ff_3 (
    .clk(clock), .D(D[2]), .Q(Q[2]), .en(write), .reset(reset));  // open: Qn, preset
  D_Flip_Flop #(.trigger("falling")) d_ff_4 (.clk(clock), .D(D[3]), .Q(Q[3]), .reset(reset));  // open: Qn, preset, en
  D_Flip_Flop #(.trigger("falling")) d_ff_5 (
    .clk(clock), .D(D[4]), .Q(Q[4]), .en(write), .reset(reset));  // open: Qn, preset
  D_Flip_Flop #(.trigger("falling")) d_ff_6 (
    .clk(clock), .D(D[5]), .Q(Q[5]), .en(write), .reset(reset));  // open: Qn, preset
  D_Flip_Flop #(.trigger("falling")) d_ff_7 (
    .clk(clock), .D(D[6]), .Q(Q[6]), .en(write), .reset(reset));  // open: Qn, preset
  D_Flip_Flop #(.trigger("falling")) d_ff_8 (
    .clk(clock), .D(D[7]), .Q(Q[7]), .en(write), .reset(reset));  // open: Qn, preset
  D_Flip_Flop #(.trigger("falling")) d_ff_9 (
    .clk(clock), .D(D[8]), .Q(Q[8]), .en(write), .reset(reset));  // open: Qn, preset
  D_Flip_Flop #(.trigger("falling")) d_ff_10 (
    .clk(clock), .D(D[9]), .Q(Q[9]), .en(write), .reset(reset));  // open: Qn, preset
  D_Flip_Flop #(.trigger("falling")) d_ff_11 (
    .clk(clock), .D(D[10]), .Q(Q[10]), .en(write), .reset(reset));  // open: Qn, preset
  D_Flip_Flop #(.trigger("falling")) d_ff_12 (
    .clk(clock), .D(D[11]), .Q(Q[11]), .en(write), .reset(reset));  // open: Qn, preset
  D_Flip_Flop #(.trigger("falling")) d_ff_13 (
    .clk(clock), .D(D[12]), .Q(Q[12]), .en(write), .reset(reset));  // open: Qn, preset
  D_Flip_Flop #(.trigger("falling")) d_ff_14 (
    .clk(clock), .D(D[13]), .Q(Q[13]), .en(write), .reset(reset));  // open: Qn, preset
  D_Flip_Flop #(.trigger("falling")) d_ff_15 (
    .clk(clock), .D(D[14]), .Q(Q[14]), .en(write), .reset(reset));  // open: Qn, preset
  D_Flip_Flop #(.trigger("falling")) d_ff_16 (
    .clk(clock), .D(D[15]), .Q(Q[15]), .en(write), .reset(reset));  // open: Qn, preset
endmodule

module register_file (
  input  write,
  input  [2:0] rd,
  input  reset,
  input  clock,
  input  [2:0] rs,
  input  [2:0] rt,
  input  [15:0] Data,
  output [15:0] out_8,
  output [15:0] out_9
);

  wire demultiplexer_1_out1, demultiplexer_1_out2, demultiplexer_1_out3, demultiplexer_1_out4,
       demultiplexer_1_out5, demultiplexer_1_out6, demultiplexer_1_out7;
  wire [15:0] n16_bit_register_1_q, n16_bit_register_2_q, n16_bit_register_3_q, n16_bit_register_4_q,
       n16_bit_register_5_q, n16_bit_register_6_q, n16_bit_register_7_q;

  Demultiplexer #(.select(3), .enable("false")) demultiplexer_1 (
    .out1(demultiplexer_1_out1), .out2(demultiplexer_1_out2), .out3(demultiplexer_1_out3),
    .out4(demultiplexer_1_out4), .out5(demultiplexer_1_out5), .out6(demultiplexer_1_out6),
    .out7(demultiplexer_1_out7), .in(write), .sel(rd));  // open: out0
  _16_bit_register u_16_bit_register_1 (
    .D(Data), .reset(reset), .write(demultiplexer_1_out1), .clock(clock), .Q(n16_bit_register_1_q));
  _16_bit_register u_16_bit_register_2 (
    .D(Data), .reset(reset), .write(demultiplexer_1_out2), .clock(clock), .Q(n16_bit_register_2_q));
  _16_bit_register u_16_bit_register_3 (
    .D(Data), .reset(reset), .write(demultiplexer_1_out3), .clock(clock), .Q(n16_bit_register_3_q));
  _16_bit_register u_16_bit_register_4 (
    .D(Data), .reset(reset), .write(demultiplexer_1_out4), .clock(clock), .Q(n16_bit_register_4_q));
  _16_bit_register u_16_bit_register_5 (
    .D(Data), .reset(reset), .write(demultiplexer_1_out5), .clock(clock), .Q(n16_bit_register_5_q));
  _16_bit_register u_16_bit_register_6 (
    .D(Data), .reset(reset), .write(demultiplexer_1_out6), .clock(clock), .Q(n16_bit_register_6_q));
  _16_bit_register u_16_bit_register_7 (
    .D(Data), .reset(reset), .write(demultiplexer_1_out7), .clock(clock), .Q(n16_bit_register_7_q));
  Multiplexer #(.select(3), .width(16), .enable("false")) multiplexer_1 (
    .in0({16{1'b0}}), .in1(n16_bit_register_1_q), .in2(n16_bit_register_2_q), .in3(n16_bit_register_3_q),
    .in4(n16_bit_register_4_q), .in5(n16_bit_register_5_q), .in6(n16_bit_register_6_q),
    .in7(n16_bit_register_7_q), .out(out_8), .sel(rs));
  Multiplexer #(.select(3), .width(16), .enable("false")) multiplexer_2 (
    .in0({16{1'b0}}), .in1(n16_bit_register_1_q), .in2(n16_bit_register_2_q), .in3(n16_bit_register_3_q),
    .in4(n16_bit_register_4_q), .in5(n16_bit_register_5_q), .in6(n16_bit_register_6_q),
    .in7(n16_bit_register_7_q), .out(out_9), .sel(rt));
endmodule

module _16_bit_counter (
  input  reset,
  input  [15:0] \input ,
  input  [3:0] ALU_code,
  input  clock,
  output [15:0] \output 
);

  wire comparator_1_eq, or_1_out;
  wire [15:0] n16_bit_alu_1_result;

  _16_bit_ALU u_16_bit_alu_1 (
    .ALU_code(ALU_code), .a(\output ), .b(16'h1), .result(n16_bit_alu_1_result));  // open: overflow
  _16_bit_register u_16_bit_register_1 (
    .D(n16_bit_alu_1_result), .reset(or_1_out), .write(1'b1), .clock(clock), .Q(\output ));
  Comparator #(.width(16)) comparator_1 (.a(\input ), .b(\output ), .eq(comparator_1_eq));  // open: gt, lt
  or or_1 (or_1_out, comparator_1_eq, reset);
endmodule

module traffic_lite (
);

  wire and_1_out, and_2_out, and_3_out, and_4_out, and_5_out, and_6_out, clock_1_out, comparator_1_lt,
       comparator_2_lt, comparator_3_lt, comparator_4_lt, comparator_5_lt, not_1_out, not_2_out, not_3_out,
       not_4_out, not_5_out, not_6_out, not_7_out, not_8_out, not_9_out, or_1_out;
  wire [15:0] n16_bit_counter_1_output;

  // Probe on n16_bit_counter_1_output
  Clock clock_1 (.out(clock_1_out));
  _16_bit_counter u_16_bit_counter_1 (
    .\input (16'h1c), .ALU_code(4'b0100), .clock(clock_1_out), .\output (n16_bit_counter_1_output));  // open: reset
  Comparator #(.width(16)) comparator_1 (
    .a(n16_bit_counter_1_output), .b(16'h8), .lt(comparator_1_lt));  // open: gt, eq
  Comparator #(.width(16)) comparator_2 (
    .a(n16_bit_counter_1_output), .b(16'hc), .lt(comparator_2_lt));  // open: gt, eq
  Comparator #(.width(16)) comparator_3 (
    .a(n16_bit_counter_1_output), .b(16'he), .lt(comparator_3_lt));  // open: gt, eq
  Comparator #(.width(16)) comparator_4 (
    .a(n16_bit_counter_1_output), .b(16'h16), .lt(comparator_4_lt));  // open: gt, eq
  Comparator #(.width(16)) comparator_5 (
    .a(n16_bit_counter_1_output), .b(16'h1a), .lt(comparator_5_lt));  // open: gt, eq
  and and_1 (and_1_out, comparator_2_lt, not_1_out);
  not not_1 (not_1_out, comparator_1_lt);
  and and_2 (and_2_out, comparator_3_lt, comparator_4_lt, comparator_5_lt);
  and and_3 (and_3_out, comparator_5_lt, not_2_out, not_3_out);
  not not_2 (not_2_out, comparator_4_lt);
  not not_3 (not_3_out, comparator_3_lt);
  not not_4 (not_4_out, comparator_5_lt);
  not not_5 (not_5_out, comparator_4_lt);
  and and_4 (and_4_out, not_4_out, not_5_out, not_6_out);
  not not_6 (not_6_out, comparator_3_lt);
  not not_7 (not_7_out, and_1_out);
  and and_5 (and_5_out, not_7_out, not_8_out);
  not not_8 (not_8_out, comparator_1_lt);
  or or_1 (or_1_out, and_2_out, and_4_out);
  not not_9 (not_9_out, and_2_out);
  and and_6 (and_6_out, not_9_out, comparator_4_lt, comparator_5_lt);
  LED led_1 (.in(and_5_out));
  LED led_2 (.in(and_1_out));
  LED led_3 (.in(comparator_1_lt));
  LED led_4 (.in(or_1_out));
  LED led_5 (.in(and_3_out));
  LED led_6 (.in(and_6_out));
endmodule

module _16_bit_stack (
  input  reset,
  input  [15:0] Data,
  input  pop,
  input  push,
  output [15:0] out_5,
  output error
);

  wire and_1_out, and_3_out, clock_1_out, comparator_1_eq, multiplexer_4_out, nand_1_out, or_1_out, or_2_out;
  wire [3:0] multiplexer_2_out;
  wire [15:0] multiplexer_1_out, multiplexer_3_out, multiplexer_5_out, n16_bit_counter_1_output,
       subtractor_1_out;

  Multiplexer #(.width(16), .enable("false")) multiplexer_1 (
    .in0({16{1'b1}}), .in1({16{1'b0}}), .out(multiplexer_1_out), .sel(pop));
  Multiplexer #(.width(4), .enable("false")) multiplexer_2 (
    .in0(4'b0100), .in1(4'b0101), .out(multiplexer_2_out), .sel(pop));
  _16_bit_counter u_16_bit_counter_1 (
    .reset(reset), .\input (multiplexer_1_out), .ALU_code(multiplexer_2_out), .clock(or_1_out),
    .\output (n16_bit_counter_1_output));
  Multiplexer #(.width(16), .enable("false")) multiplexer_3 (
    .in0(Data), .in1({16{1'b0}}), .out(multiplexer_3_out), .sel(pop));
  or or_1 (or_1_out, and_1_out, and_3_out);
  and and_1 (and_1_out, pop, clock_1_out);
  Clock clock_1 (.out(clock_1_out));
  and and_2 (error, pop, push);
  and and_3 (and_3_out, clock_1_out, push);
  Comparator #(.width(16)) comparator_1 (
    .a(n16_bit_counter_1_output), .b({16{1'b0}}), .eq(comparator_1_eq));  // open: gt, lt
  Subtractor #(.width(16)) subtractor_1 (
    .a(n16_bit_counter_1_output), .b(16'h1), .out(subtractor_1_out));  // open: bin, bout
  Multiplexer #(.select(2), .enable("false")) multiplexer_4 (
    .in0(nand_1_out), .in1(1'b0), .in2(nand_1_out), .out(multiplexer_4_out), .sel({pop, push}));  // open: in3
  nand nand_1 (nand_1_out, comparator_1_eq, 1'b1);
  Multiplexer #(.width(16), .enable("false")) multiplexer_5 (
    .in0(n16_bit_counter_1_output), .in1(subtractor_1_out), .out(multiplexer_5_out), .sel(multiplexer_4_out));
  or or_2 (or_2_out, pop, push);
  RAM #(.addrWidth(16), .dataWidth(16), .bus("separate")) ram_1 (
    .addr(multiplexer_5_out), .din(multiplexer_3_out), .data(out_5), .str(or_2_out), .clk(or_1_out),
    .clr(reset));  // open: sel, ld
endmodule
