// Logisim project SD_Group01.circ as structural Verilog: 6 circuits, main circuit main
module main (
  output [15:0] pc,
  output [15:0] r0,
  output [15:0] r1,
  output [15:0] r2,
  output [15:0] r3,
  output [15:0] r4,
  output [15:0] r5,
  output [15:0] r6,
  output [15:0] r7,
  output halt
);

  wire clk, clock_1_out, ImmOp, inc_dec, lui, MemOp, rst, sw;
  wire [2:0] control_unit_1_rd, control_unit_1_rs, control_unit_1_rt, multiplexer_1_out;
  wire [3:0] ALU_Code;
  wire [15:0] multiplexer_2_out, multiplexer_3_out, multiplexer_4_out, multiplexer_5_out, multiplexer_6_out,
       n16_bit_alu_1_result, ram_1_data, ram_2_data, register_file_1_out_8, register_file_1_out_9,
       signed_imm, unsigned_imm;

  Halt halt_1 (.instruction(ram_1_data), .clock(clock_1_out), .reset(rst), .halt(halt));
  Clock clock_1 (.out(clock_1_out));
  Button reset (.out(rst));
  and and_1 (clk, ~halt, clock_1_out);  // AND_Gate
  PC pc_1 (
    .Branch__Value({16{1'b0}}), .Reset(rst), .Instruction_Address(pc), .Branch_Relative(1'b0),
    .Branch_Absolute(1'b0), .Clock(clk));
  RAM #(.addrWidth(16), .dataWidth(16), .bus("asynch")) ram_1 (.addr(pc), .data(ram_1_data));  // open: sel, ld, clr
  Control_Unit control_unit_1 (
    .instruction(ram_1_data), .ALU_code(ALU_Code), .rd(control_unit_1_rd), .rs(control_unit_1_rs),
    .rt(control_unit_1_rt), .signed_imm(signed_imm), .lw_sq(sw), .MemOp(MemOp), .ImmOp(ImmOp),
    .unsigned_imm(unsigned_imm), .lui(lui), .inc_dec(inc_dec));
  Multiplexer #(.width(3), .enable("false")) multiplexer_1 (
    .in0(control_unit_1_rs), .in1(control_unit_1_rd), .out(multiplexer_1_out), .sel(ImmOp));
  Register_File register_file_1 (
    .Data(multiplexer_6_out), .write(1'b1), .rd(control_unit_1_rd), .reset(rst), .clock(clk),
    .rs(multiplexer_1_out), .out_8(register_file_1_out_8), .rt(control_unit_1_rt),
    .out_9(register_file_1_out_9), .r0(r0), .r1(r1), .r2(r2), .r3(r3), .r4(r4), .r5(r5), .r6(r6), .r7(r7));
  Multiplexer #(.width(16), .enable("false")) multiplexer_2 (
    .in0(register_file_1_out_9), .in1(signed_imm), .out(multiplexer_2_out), .sel(MemOp));
  Multiplexer #(.width(16), .enable("false")) multiplexer_3 (
    .in0(multiplexer_2_out), .in1(unsigned_imm), .out(multiplexer_3_out), .sel(ImmOp));
  Multiplexer #(.width(16), .enable("false")) multiplexer_4 (
    .in0(register_file_1_out_8), .in1({unsigned_imm[7:0], {8{1'b0}}}), .out(multiplexer_4_out), .sel(lui));
  Multiplexer #(.width(16), .enable("false")) multiplexer_5 (
    .in0(multiplexer_3_out), .in1(16'h1), .out(multiplexer_5_out), .sel(inc_dec));
  _16_bit_ALU u_16_bit_alu_1 (
    .ALU_code(ALU_Code), .a(multiplexer_4_out), .b(multiplexer_5_out), .result(n16_bit_alu_1_result));  // open: overflow
  Multiplexer #(.width(16), .enable("false")) multiplexer_6 (
    .in0(n16_bit_alu_1_result), .in1(ram_2_data), .out(multiplexer_6_out), .sel(MemOp));
  RAM #(.addrWidth(16), .dataWidth(16), .bus("separate")) ram_2 (
    .addr(n16_bit_alu_1_result), .din(multiplexer_4_out), .data(ram_2_data), .str(sw), .clk(clk), .ld(1'b1));  // open: sel, clr

  // Notes on the sheet:
  //   current instruction
  //   clock signal
  //   reset button
  //   DO NOT CHANGE THE INPUTS AND OUTPUTS OF THIS CIRCUIT! Do not add/remove inputs or outputs. Do not even change their location or orientation.
endmodule

module Halt (
  input  [15:0] instruction,
  input  clock,
  input  reset,
  output halt
);

  wire and_1_out, comparator_1_eq, comparator_2_gt, counter_1_carry, or_1_out, or_2_out;
  wire [11:0] counter_1_q;

  Comparator #(.width(16), .mode("unsigned")) comparator_1 (
    .a(instruction), .b({16{1'b0}}), .eq(comparator_1_eq));  // open: gt, lt
  Counter #(.width(12), .max('hfff), .trigger("falling")) counter_1 (
    .Q(counter_1_q), .carry(counter_1_carry), .clk(clock), .clr(reset));  // open: load, D, count
  or or_1 (or_1_out, comparator_1_eq, counter_1_carry);
  Comparator #(.width(12), .mode("unsigned")) comparator_2 (
    .a(counter_1_q), .b({12{1'b0}}), .gt(comparator_2_gt));  // open: eq, lt
  or or_2 (or_2_out, halt, and_1_out);
  and and_1 (and_1_out, or_1_out, comparator_2_gt);
  Register_part #(.width(1)) register_1 (.D(or_2_out), .Q(halt), .clk(clock), .clr(reset));  // open: en

  // Notes on the sheet:
  //   halt becomes and stays asserted if the instruction is 0000 (not in the first clock cycle) or the end of the counter is reached (2^12)
endmodule

module Register (
  input  reset,
  input  write,
  input  clock,
  input  [15:0] D,
  output [15:0] Q
);

  D_Flip_Flop #(.trigger("falling")) d_ff_1 (
    .clk(clock), .D(D[0]), .Q(Q[0]), .en(write), .reset(reset));  // open: Qn, preset
  D_Flip_Flop #(.trigger("falling")) d_ff_2 (
    .clk(clock), .D(D[1]), .Q(Q[1]), .en(write), .reset(reset));  // open: Qn, preset
  D_Flip_Flop #(.trigger("falling")) d_ff_3 (
    .clk(clock), .D(D[2]), .Q(Q[2]), .en(write), .reset(reset));  // open: Qn, preset
  D_Flip_Flop #(.trigger("falling")) d_ff_4 (
    .clk(clock), .D(D[3]), .Q(Q[3]), .en(write), .reset(reset));  // open: Qn, preset
  D_Flip_Flop #(.trigger("falling")) d_ff_5 (
    .clk(clock), .D(D[4]), .Q(Q[4]), .en(write), .reset(reset));  // open: Qn, preset
  D_Flip_Flop #(.trigger("falling")) d_ff_6 (
    .clk(clock), .D(D[5]), .Q(Q[5]), .en(write), .reset(reset));  // open: Qn, preset
  D_Flip_Flop #(.trigger("falling")) d_ff_7 (
    .clk(clock), .D(D[6]), .Q(Q[6]), .en(write), .reset(reset));  // open: Qn, preset
  D_Flip_Flop #(.trigger("falling")) d_ff_8 (
    .clk(clock), .D(D[7]), .Q(Q[7]), .en(write), .reset(reset));  // open: Qn, preset
  D_Flip_Flop #(.trigger("falling")) d_ff_9 (
    .clk(clock), .D(D[8]), .Q(Q[8]), .en(write), .reset(reset));  // open: Qn, preset
  D_Flip_Flop #(.trigger("falling")) d_ff_10 (
    .clk(clock), .D(D[9]), .Q(Q[9]), .en(write), .reset(reset));  // open: Qn, preset
  D_Flip_Flop #(.trigger("falling")) d_ff_11 (
    .clk(clock), .D(D[10]), .Q(Q[10]), .en(write), .reset(reset));  // open: Qn, preset
  D_Flip_Flop #(.trigger("falling")) d_ff_12 (
    .clk(clock), .D(D[11]), .Q(Q[11]), .en(write), .reset(reset));  // open: Qn, preset
  D_Flip_Flop #(.trigger("falling")) d_ff_13 (
    .clk(clock), .D(D[12]), .Q(Q[12]), .en(write), .reset(reset));  // open: Qn, preset
  D_Flip_Flop #(.trigger("falling")) d_ff_14 (
    .clk(clock), .D(D[13]), .Q(Q[13]), .en(write), .reset(reset));  // open: Qn, preset
  D_Flip_Flop #(.trigger("falling")) d_ff_15 (
    .clk(clock), .D(D[14]), .Q(Q[14]), .en(write), .reset(reset));  // open: Qn, preset
  D_Flip_Flop #(.trigger("falling")) d_ff_16 (
    .clk(clock), .D(D[15]), .Q(Q[15]), .en(write), .reset(reset));  // open: Qn, preset
endmodule

module PC (
  input  Branch_Relative,
  input  Branch_Absolute,
  input  Clock,
  input  [15:0] Branch__Value,
  input  Reset,
  output [15:0] Instruction_Address
);

  wire and_1_out, nand_1_out, not_1_out, not_2_out, or_1_out;
  wire [15:0] adder_1_out, multiplexer_1_out, multiplexer_2_out;

  Multiplexer #(.width(16), .enable("false")) multiplexer_1 (
    .in0({16{1'b0}}), .in1(Branch__Value), .out(multiplexer_1_out), .sel(Branch_Relative));
  not not_1 (not_1_out, Branch_Relative);
  not not_2 (not_2_out, Branch_Absolute);
  and and_1 (and_1_out, not_1_out, not_2_out);
  or or_1 (or_1_out, Branch_Relative, and_1_out);
  Adder #(.width(16)) adder_1 (
    .a(multiplexer_1_out), .b(Instruction_Address), .out(adder_1_out), .cin(or_1_out));  // open: cout
  Multiplexer #(.width(16), .enable("false")) multiplexer_2 (
    .in0(adder_1_out), .in1(Branch__Value), .out(multiplexer_2_out), .sel(Branch_Absolute));
  nand nand_1 (nand_1_out, Branch_Relative, Branch_Absolute);
  Register register_1 (
    .D(multiplexer_2_out), .reset(Reset), .write(nand_1_out), .clock(Clock), .Q(Instruction_Address));
endmodule

module Register_File (
  input  write,
  input  [2:0] rd,
  input  reset,
  input  clock,
  input  [2:0] rs,
  input  [2:0] rt,
  input  [15:0] Data,
  output [15:0] out_8,
  output [15:0] out_9,
  output [15:0] r0,
  output [15:0] r1,
  output [15:0] r2,
  output [15:0] r3,
  output [15:0] r4,
  output [15:0] r5,
  output [15:0] r6,
  output [15:0] r7
);

  wire demultiplexer_1_out1, demultiplexer_1_out2, demultiplexer_1_out3, demultiplexer_1_out4,
       demultiplexer_1_out5, demultiplexer_1_out6, demultiplexer_1_out7;

  Demultiplexer #(.select(3), .enable("false")) demultiplexer_1 (
    .out1(demultiplexer_1_out1), .out2(demultiplexer_1_out2), .out3(demultiplexer_1_out3),
    .out4(demultiplexer_1_out4), .out5(demultiplexer_1_out5), .out6(demultiplexer_1_out6),
    .out7(demultiplexer_1_out7), .in(write), .sel(rd));  // open: out0
  Register register_1 (.D(Data), .reset(reset), .write(demultiplexer_1_out1), .clock(clock), .Q(r1));
  Register register_2 (.D(Data), .reset(reset), .write(demultiplexer_1_out2), .clock(clock), .Q(r2));
  Register register_3 (.D(Data), .reset(reset), .write(demultiplexer_1_out3), .clock(clock), .Q(r3));
  Register register_4 (.D(Data), .reset(reset), .write(demultiplexer_1_out4), .clock(clock), .Q(r4));
  Register register_5 (.D(Data), .reset(reset), .write(demultiplexer_1_out5), .clock(clock), .Q(r5));
  Register register_6 (.D(Data), .reset(reset), .write(demultiplexer_1_out6), .clock(clock), .Q(r6));
  Register register_7 (.D(Data), .reset(reset), .write(demultiplexer_1_out7), .clock(clock), .Q(r7));
  Multiplexer #(.select(3), .width(16), .enable("false")) multiplexer_1 (
    .in0({16{1'b0}}), .in1(r1), .in2(r2), .in3(r3), .in4(r4), .in5(r5), .in6(r6), .in7(r7), .out(out_8),
    .sel(rs));
  Multiplexer #(.select(3), .width(16), .enable("false")) multiplexer_2 (
    .in0({16{1'b0}}), .in1(r1), .in2(r2), .in3(r3), .in4(r4), .in5(r5), .in6(r6), .in7(r7), .out(out_9),
    .sel(rt));

  assign r0 = {16{1'b0}};
endmodule

module Control_Unit (
  input  [15:0] instruction,
  output MemOp,
  output ImmOp,
  output [3:0] ALU_code,
  output [2:0] rd,
  output [2:0] rs,
  output [2:0] rt,
  output [15:0] signed_imm,
  output [15:0] unsigned_imm,
  output lw_sq,
  output lui,
  output inc_dec
);

  wire check, comparator_1_eq, comparator_2_eq, comparator_3_eq, not_1_out, not_2_out, or_1_out;
  wire [3:0] multiplexer_1_out;
  wire [15:0] signed_imm_t, unsigned_imm_t;

  Multiplexer #(.select(2), .width(4), .enable("false")) multiplexer_1 (
    .in0(4'b0011), .in1(4'b1111), .in2(4'b0100), .in3(4'b0101), .out(multiplexer_1_out),
    .sel(instruction[12:11]));
  not not_1 (not_1_out, instruction[15]);
  and and_1 (check, not_1_out, not_2_out);
  not not_2 (not_2_out, instruction[14]);
  Multiplexer #(.select(3), .width(4), .enable("false")) multiplexer_2 (
    .in0(instruction[12:9]), .in1(instruction[12:9]), .in2(instruction[12:9]), .in3(4'b0100),
    .in4(multiplexer_1_out), .out(ALU_code), .sel(instruction[15:13]));  // open: in5, in6, in7
  Comparator #(.width(2)) comparator_1 (.a(instruction[12:11]), .b(2'b01), .eq(comparator_1_eq));  // open: gt, lt
  Comparator #(.width(4)) comparator_2 (.a(ALU_code), .b(4'b0100), .eq(comparator_2_eq));  // open: gt, lt
  Comparator #(.width(4)) comparator_3 (.a(ALU_code), .b(4'b0101), .eq(comparator_3_eq));  // open: gt, lt
  and and_2 (lui, instruction[15], comparator_1_eq);
  Multiplexer #(.select(3), .width(3), .enable("false")) multiplexer_3 (
    .in0(instruction[8:6]), .in1(instruction[8:6]), .in2(instruction[8:6]), .in3(instruction[11:9]),
    .in4(instruction[10:8]), .out(rd), .sel(instruction[15:13]));  // open: in5, in6, in7
  and and_3 (inc_dec, check, or_1_out);
  or or_1 (or_1_out, comparator_2_eq, comparator_3_eq);
  Multiplexer #(.select(3), .width(3), .enable("false")) multiplexer_4 (
    .in0(3'b000), .in1(instruction[5:3]), .in2(instruction[5:3]), .in3(instruction[8:6]), .in4(3'b000),
    .out(rs), .sel(instruction[15:13]));  // open: in5, in6, in7
  and and_4 (MemOp, instruction[14], instruction[13]);
  Multiplexer #(.select(3), .width(3), .enable("false")) multiplexer_5 (
    .in0(3'b000), .in1(3'b000), .in2(instruction[2:0]), .in3(3'b000), .in4(3'b000), .out(rt),
    .sel(instruction[15:13]));  // open: in5, in6, in7
  assign signed_imm_t = {{10{instruction[5]}}, instruction[5:0]};  // Bit_Extender bit_extender_1
  Multiplexer #(.select(3), .width(16), .enable("false")) multiplexer_6 (
    .in0({16{1'b0}}), .in1({16{1'b0}}), .in2({16{1'b0}}), .in3(signed_imm_t), .in4({16{1'b0}}),
    .out(signed_imm), .sel(instruction[15:13]));  // open: in5, in6, in7
  Multiplexer #(.select(3), .enable("false")) multiplexer_7 (
    .in0(1'b0), .in1(1'b0), .in2(1'b0), .in3(instruction[12]), .in4(1'b0), .out(lw_sq),
    .sel(instruction[15:13]));  // open: in5, in6, in7
  assign unsigned_imm_t = {{8{1'b0}}, instruction[7:0]};  // Bit_Extender bit_extender_2
  Multiplexer #(.select(3), .width(16), .enable("false")) multiplexer_8 (
    .in0({16{1'b0}}), .in1({16{1'b0}}), .in2({16{1'b0}}), .in3({16{1'b0}}), .in4(unsigned_imm_t),
    .out(unsigned_imm), .sel(instruction[15:13]));  // open: in5, in6, in7

  assign ImmOp = instruction[15];

  // Other names for the same wires on the sheet: rt2[2:0] = instruction[2:0]; rs1[2:0] = instruction[5:3];
  //   rs2[2:0] = instruction[5:3]; rd0[2:0] = instruction[8:6]; rd1[2:0] = instruction[8:6];
  //   rd2[2:0] = instruction[8:6]; rs3[2:0] = instruction[8:6]; ALU[3:0] = ALU_code; ALU0[3:0] = instruction[12:9];
  //   ALU1[3:0] = instruction[12:9]; ALU2[3:0] = instruction[12:9]; op_code[1:0] = instruction[12:11];
  //   rd3[2:0] = instruction[11:9]; lw_sw = instruction[12]; rd4[2:0] = instruction[10:8]

  // Notes on the sheet:
  //   ZERO
  //   UNARY
  //   BINARY
  //   LW/SW
  //   IMMEDIATE OP
endmodule
